// Digital circuit LEG.dig as structural Verilog
module LEG (
  input  C_0,
  input  C_1,
  input  C_2,
  input  [7:0] A_0,
  input  [7:0] B_0,
  input  clk,
  input  [7:0] Num_1,
  input  In_3,
  input  In_2,
  input  In_1,
  input  C_3,
  input  C_4,
  input  C_5,
  output Out_0,
  output [7:0] C_Arith
);

  wire and_1_out, and_2_out, and_3_out, and_4_out, and_5_out, and_6_out, and_7_out, and_8_out, and_9_out,
       and_10_out, and_11_out, and_12_out, and_13_out, and_14_out, and_15_out, and_16_out, and_17_out,
       and_18_out, and_19_out, and_20_out, and_21_out, and_22_out, and_23_out, and_24_out, and_25_out,
       and_26_out, and_27_out, and_28_out, and_29_out, and_30_out, and_31_out, and_32_out, and_33_out,
       and_34_out, and_35_out, and_36_out, and_37_out, and_38_out, and_39_out, and_40_out, and_41_out,
       and_42_out, and_43_out, and_44_out, and_45_out, and_46_out, and_47_out, and_48_out, and_49_out,
       and_50_out, and_51_out, and_52_out, and_53_out, and_54_out, and_55_out, and_56_out, and_57_out,
       and_58_out, and_59_out, and_60_out, and_61_out, and_62_out, and_63_out, and_64_out, and_65_out,
       and_66_out, and_67_out, and_68_out, and_69_out, and_70_out, and_71_out, and_72_out, and_73_out,
       and_74_out, and_81_out, and_82_out, and_83_out, and_84_out, and_85_out, and_86_out, and_87_out,
       and_88_out, and_91_out, and_92_out, and_93_out, and_94_out, and_95_out, and_96_out, and_97_out,
       and_98_out, and_99_out, and_100_out, and_101_out, and_102_out, and_103_out, and_104_out, and_105_out,
       and_106_out, and_107_out, and_108_out, and_109_out, and_110_out, and_111_out, and_112_out,
       and_113_out, and_116_out, and_117_out, and_118_out, and_119_out, and_120_out, and_121_out,
       and_122_out, and_123_out, and_126_out, and_127_out, and_128_out, and_129_out, and_131_out,
       and_132_out, and_133_out, and_134_out, and_147_out, and_148_out, and_149_out, and_150_out,
       and_151_out, and_152_out, and_153_out, and_154_out, and_155_out, and_156_out, and_157_out,
       and_158_out, and_159_out, and_160_out, and_161_out, and_162_out, and_163_out, and_164_out,
       and_165_out, and_166_out, and_167_out, and_168_out, and_169_out, and_171_out, and_172_out,
       and_173_out, and_174_out, and_181_out, and_182_out, and_183_out, and_184_out, and_185_out,
       and_186_out, and_187_out, and_188_out, and_190_out, and_191_out, and_192_out, and_193_out,
       and_195_out, and_196_out, and_197_out, and_198_out, and_199_out, and_200_out, and_201_out,
       and_202_out, and_203_out, and_204_out, and_205_out, and_206_out, and_207_out, and_208_out,
       and_209_out, and_210_out, and_211_out, and_212_out, and_213_out, and_215_out, and_216_out,
       and_217_out, and_218_out, and_219_out, and_220_out, and_221_out, and_222_out, and_223_out,
       and_224_out, and_225_out, and_226_out, and_227_out, and_228_out, and_229_out, and_230_out,
       and_231_out, and_232_out, and_233_out, and_234_out, and_235_out, and_236_out, and_237_out,
       and_238_out, and_239_out, and_240_out, and_241_out, and_242_out, and_243_out, and_244_out,
       and_245_out, and_246_out, and_247_out, and_248_out, and_249_out, and_250_out, and_251_out,
       and_252_out, and_253_out, and_254_out, and_255_out, and_256_out, and_257_out, and_258_out,
       and_259_out, and_260_out, and_261_out, and_263_out, and_264_out, and_265_out, and_266_out,
       and_267_out, and_268_out, and_269_out, and_270_out, and_271_out, and_272_out, and_273_out,
       and_274_out, and_275_out, and_276_out, and_277_out, and_278_out, and_279_out, and_280_out,
       and_281_out, and_282_out, and_283_out, and_284_out, and_285_out, and_286_out, and_287_out,
       and_288_out, and_289_out, and_290_out, and_291_out, and_292_out, and_293_out, and_294_out,
       and_295_out, and_296_out, and_297_out, dipswitch_1_out, dipswitch_2_out, dipswitch_3_out,
       dipswitch_4_out, driver_233_out, driver_234_out, driver_235_out, driver_236_out, driver_237_out,
       driver_238_out, driver_239_out, driver_240_out, driver_241_out, driver_242_out, driver_243_out,
       driver_244_out, driver_245_out, driver_246_out, driver_247_out, driver_248_out, driver_249_out,
       driver_250_out, driver_251_out, driver_252_out, driver_253_out, driver_254_out, driver_255_out,
       driver_256_out, nand_1_out, nand_2_out, nand_3_out, nand_4_out, nand_5_out, nand_6_out, nand_7_out,
       nand_8_out, nand_9_out, nand_10_out, nand_11_out, nand_12_out, nand_13_out, nand_14_out, nand_15_out,
       nand_16_out, nand_17_out, nand_18_out, nand_19_out, nand_20_out, nand_21_out, nand_22_out,
       nand_23_out, nand_24_out, nand_25_out, nand_26_out, nand_27_out, nand_28_out, nand_29_out,
       nand_30_out, nand_31_out, nand_32_out, nand_33_out, nand_34_out, nand_35_out, nand_36_out,
       nand_37_out, nand_38_out, nand_39_out, nand_40_out, nand_41_out, nand_42_out, nand_43_out,
       nand_44_out, nand_45_out, nand_46_out, nand_47_out, nand_48_out, nand_49_out, nand_50_out,
       nand_51_out, nand_52_out, nand_53_out, nand_54_out, nand_55_out, nand_56_out, nand_57_out,
       nand_58_out, nand_59_out, nand_60_out, nand_61_out, nand_62_out, nand_63_out, nand_64_out,
       nand_65_out, nand_66_out, nand_67_out, nand_68_out, nand_69_out, nand_70_out, nand_71_out,
       nand_72_out, nand_73_out, nand_74_out, nand_75_out, nand_76_out, nand_77_out, nand_78_out,
       nand_79_out, nand_80_out, nand_81_out, nand_82_out, nand_83_out, nand_84_out, nand_85_out,
       nand_86_out, nand_87_out, nand_88_out, nand_89_out, nand_90_out, nand_91_out, nand_92_out,
       nand_93_out, nand_94_out, nand_95_out, nand_96_out, nand_97_out, nand_98_out, nand_99_out,
       nand_100_out, nand_101_out, nand_102_out, nand_103_out, nand_104_out, nand_105_out, nand_106_out,
       nand_107_out, nand_108_out, nand_109_out, nand_110_out, nand_111_out, nand_112_out, nand_113_out,
       nand_114_out, nand_115_out, nand_116_out, nand_117_out, nand_118_out, nand_119_out, nand_120_out,
       nand_121_out, nand_122_out, nand_123_out, nand_124_out, nand_125_out, nand_126_out, nand_127_out,
       nand_128_out, nand_129_out, nand_130_out, nand_131_out, nand_132_out, nand_133_out, nand_134_out,
       nand_135_out, nand_136_out, nand_137_out, nand_138_out, nand_139_out, nand_140_out, nand_141_out,
       nand_142_out, nand_143_out, nand_144_out, nand_145_out, nand_146_out, nand_147_out, nand_148_out,
       nand_149_out, nand_150_out, nand_151_out, nand_152_out, nand_153_out, nand_154_out, nand_155_out,
       nand_156_out, nand_157_out, nand_158_out, nand_159_out, nand_160_out, nand_161_out, nand_162_out,
       nand_163_out, nand_164_out, nand_165_out, nand_166_out, nand_167_out, nand_168_out, nand_169_out,
       nand_170_out, nand_171_out, nand_172_out, nand_173_out, nand_174_out, nand_175_out, nand_176_out,
       nand_177_out, nand_178_out, nand_179_out, nand_180_out, nand_181_out, nand_182_out, nand_183_out,
       nand_184_out, nand_185_out, nand_186_out, nand_187_out, nand_188_out, nand_189_out, nand_190_out,
       nand_191_out, nand_192_out, nand_193_out, nand_194_out, nand_195_out, nand_196_out, nand_197_out,
       nand_198_out, nand_199_out, nand_200_out, nand_201_out, nand_202_out, nand_203_out, nand_204_out,
       nand_205_out, nand_206_out, nand_207_out, nand_208_out, nand_209_out, nand_210_out, nand_211_out,
       nand_212_out, nand_213_out, nand_214_out, nand_215_out, nand_216_out, nand_217_out, nand_218_out,
       nand_219_out, nand_220_out, nand_221_out, nand_222_out, nand_223_out, nand_224_out, nand_225_out,
       nand_226_out, nand_227_out, nand_228_out, nand_229_out, nand_230_out, nand_231_out, nand_232_out,
       nand_233_out, nand_234_out, nand_235_out, nand_236_out, nand_237_out, nand_238_out, nand_239_out,
       nand_240_out, nand_241_out, nand_242_out, nand_243_out, nand_244_out, nand_245_out, nand_246_out,
       nand_247_out, nand_248_out, nand_249_out, nand_250_out, nand_251_out, nand_252_out, nand_253_out,
       nand_254_out, nand_255_out, nand_256_out, nand_257_out, nand_258_out, nand_259_out, nand_260_out,
       nand_261_out, nand_262_out, nand_263_out, nand_264_out, nand_265_out, nand_266_out, nand_267_out,
       nand_268_out, nand_269_out, nand_270_out, nand_271_out, nand_272_out, nand_273_out, nand_274_out,
       nand_275_out, nand_276_out, nand_277_out, nand_278_out, nand_279_out, nand_280_out, nand_281_out,
       nand_282_out, nand_283_out, nand_284_out, nand_285_out, nand_286_out, nand_287_out, nand_288_out,
       nand_297_out, nand_298_out, nand_299_out, nand_300_out, nand_301_out, nand_302_out, nand_303_out,
       nand_304_out, nand_305_out, nand_306_out, nand_307_out, nand_308_out, nand_309_out, nand_310_out,
       nand_311_out, nand_312_out, nand_314_out, nand_316_out, nand_318_out, nand_320_out, nand_321_out,
       nand_322_out, nand_323_out, nand_324_out, nand_325_out, nand_326_out, nand_327_out, nand_328_out,
       nand_329_out, nand_330_out, nand_331_out, nand_332_out, nand_333_out, nand_334_out, nand_335_out,
       nand_336_out, nand_338_out, nand_340_out, nand_342_out, nand_344_out, nand_353_out, nand_354_out,
       nand_355_out, nand_356_out, nand_357_out, nand_358_out, nand_359_out, nand_360_out, nand_361_out,
       nand_362_out, nand_363_out, nand_364_out, nand_365_out, nand_366_out, nand_367_out, nand_368_out,
       nand_369_out, nand_370_out, nand_371_out, nand_372_out, nand_373_out, nand_374_out, nand_375_out,
       nand_376_out, nand_377_out, nand_378_out, nand_379_out, nand_380_out, nand_381_out, nand_382_out,
       nand_383_out, nand_384_out, nand_385_out, nand_386_out, nand_387_out, nand_388_out, nand_389_out,
       nand_390_out, nand_391_out, nand_392_out, nand_393_out, nand_394_out, nand_395_out, nand_396_out,
       nand_397_out, nand_398_out, nand_399_out, nand_400_out, nand_401_out, nand_402_out, nand_403_out,
       nand_404_out, nand_405_out, nand_406_out, nand_407_out, nand_408_out, nor_17_out, nor_18_out,
       nor_19_out, nor_20_out, nor_21_out, nor_22_out, nor_23_out, nor_24_out, nor_25_out, nor_26_out,
       nor_27_out, nor_28_out, nor_29_out, nor_30_out, nor_31_out, nor_32_out, nor_33_out, nor_34_out,
       nor_35_out, nor_36_out, nor_37_out, nor_38_out, nor_39_out, nor_40_out, nor_41_out, nor_42_out,
       not_1_out, not_2_out, not_3_out, not_4_out, not_5_out, not_6_out, not_7_out, not_8_out, not_9_out,
       not_10_out, not_11_out, not_12_out, not_13_out, not_14_out, not_15_out, not_16_out, not_17_out,
       not_18_out, not_19_out, not_20_out, not_21_out, not_22_out, not_23_out, not_24_out, not_25_out,
       not_26_out, not_27_out, not_28_out, not_29_out, not_30_out, not_31_out, not_32_out, not_33_out,
       not_34_out, not_35_out, not_36_out, not_37_out, not_38_out, not_39_out, not_40_out, not_41_out,
       not_42_out, not_43_out, not_44_out, not_45_out, not_46_out, not_47_out, not_48_out, not_49_out,
       not_50_out, not_51_out, not_52_out, not_53_out, not_54_out, not_55_out, not_56_out, not_57_out,
       not_58_out, not_59_out, not_60_out, not_61_out, not_62_out, not_63_out, not_64_out, not_65_out,
       not_66_out, not_67_out, notconnected_1_out, notconnected_8_out, notconnected_10_out,
       notconnected_11_out, notconnected_14_out, notconnected_15_out, notconnected_16_out,
       notconnected_18_out, notconnected_23_out, notconnected_27_out, notconnected_28_out,
       notconnected_29_out, notconnected_30_out, notconnected_32_out, or_8_out, or_9_out, or_10_out,
       or_11_out, or_12_out, or_13_out, or_14_out, or_15_out, or_18_out, or_19_out, or_20_out, or_21_out,
       or_22_out, or_23_out, or_24_out, or_25_out, or_34_out, or_35_out, or_36_out, or_37_out, or_38_out,
       or_39_out, or_40_out, or_41_out, or_42_out, or_43_out, or_44_out, or_45_out, or_46_out, or_47_out,
       or_48_out, or_50_out, or_51_out, or_59_out, or_60_out, or_61_out, or_62_out, or_63_out, or_64_out,
       or_65_out, or_66_out, or_68_out, or_69_out, or_70_out, or_71_out, or_72_out, or_73_out, or_74_out,
       or_75_out, or_76_out, or_77_out, or_78_out, or_79_out, or_80_out, or_81_out, or_82_out, or_83_out,
       or_84_out, xor_1_out, xor_2_out, xor_3_out, xor_4_out, xor_5_out, xor_6_out, xor_7_out, xor_8_out,
       xor_15_out, xor_16_out, xor_17_out, xor_18_out, xor_19_out, xor_20_out, xor_21_out, xor_22_out,
       xor_33_out, xor_34_out, xor_35_out, xor_36_out, xor_37_out, xor_38_out, xor_39_out, xor_40_out,
       xor_49_out, xor_50_out, xor_51_out, xor_52_out, xor_53_out, xor_54_out, xor_55_out, xor_56_out,
       xor_63_out, xor_64_out, xor_65_out, xor_66_out, xor_67_out, xor_68_out, xor_69_out, xor_70_out,
       xor_81_out, xor_82_out, xor_83_out, xor_84_out, xor_85_out, xor_86_out, xor_87_out, xor_88_out,
       xor_89_out, xor_90_out, xor_91_out, xor_92_out, xor_93_out, xor_94_out, xor_95_out, xor_96_out,
       xor_97_out, xor_98_out, xor_99_out, xor_100_out, xor_101_out, xor_102_out, xor_103_out, xor_104_out,
       xor_105_out, xor_106_out, xor_107_out, xor_108_out, xor_109_out, xor_110_out, xor_111_out, xor_112_out;
  wire [7:0] and_90_out, and_138_out, and_146_out, and_194_out, driver_1_out, driver_3_out, driver_160_out,
       nand_296_out, nand_343_out, nand_352_out, nor_8_out, nor_16_out, notconnected_2_out,
       notconnected_3_out, notconnected_4_out, notconnected_5_out, notconnected_6_out, notconnected_7_out,
       notconnected_9_out, notconnected_12_out, notconnected_13_out, notconnected_17_out,
       notconnected_19_out, notconnected_20_out, notconnected_21_out, notconnected_22_out,
       notconnected_24_out, notconnected_25_out, notconnected_26_out, notconnected_31_out, or_16_out,
       or_33_out, or_67_out, rom_1_d, xor_24_out, xor_32_out, xor_48_out, xor_76_out, xor_80_out;

  not not_1 (not_1_out, notconnected_5_out[0]);
  not not_2 (not_2_out, not_1_out);
  and and_1 (and_1_out, and_4_out, not_2_out);
  and and_2 (and_2_out, not_8_out, and_1_out);
  and and_3 (and_3_out, not_4_out, notconnected_5_out[1]);
  and and_4 (and_4_out, notconnected_5_out[1], notconnected_5_out[2]);
  and and_5 (and_5_out, and_3_out, not_2_out);
  and and_6 (and_6_out, not_8_out, and_5_out);
  and and_7 (and_7_out, notconnected_5_out[2], not_3_out);
  and and_8 (and_8_out, and_7_out, not_2_out);
  and and_9 (and_9_out, not_8_out, and_8_out);
  and and_10 (and_10_out, not_4_out, not_3_out);
  and and_11 (and_11_out, and_10_out, not_2_out);
  and and_12 (and_12_out, not_8_out, and_11_out);
  not not_3 (not_3_out, notconnected_5_out[1]);
  not not_4 (not_4_out, notconnected_5_out[2]);
  not not_5 (not_5_out, notconnected_5_out[0]);
  and and_13 (and_13_out, notconnected_5_out[1], notconnected_5_out[2]);
  and and_14 (and_14_out, and_19_out, not_5_out);
  and and_15 (and_15_out, and_13_out, not_5_out);
  and and_16 (and_16_out, not_8_out, and_14_out);
  and and_17 (and_17_out, not_8_out, and_15_out);
  and and_18 (and_18_out, notconnected_5_out[2], not_6_out);
  and and_19 (and_19_out, not_7_out, notconnected_5_out[1]);
  and and_20 (and_20_out, and_18_out, not_5_out);
  and and_21 (and_21_out, not_8_out, and_20_out);
  // NotConnected on notconnected_1_out
  and and_22 (and_22_out, not_7_out, not_6_out);
  and and_23 (and_23_out, and_22_out, not_5_out);
  and and_24 (and_24_out, not_8_out, and_23_out);
  not not_6 (not_6_out, notconnected_5_out[1]);
  not not_7 (not_7_out, notconnected_5_out[2]);
  not not_8 (not_8_out, notconnected_1_out);
  not not_9 (not_9_out, notconnected_3_out[0]);
  not not_10 (not_10_out, not_9_out);
  and and_25 (and_25_out, notconnected_3_out[1], notconnected_3_out[2]);
  and and_26 (and_26_out, and_25_out, not_10_out);
  and and_27 (and_27_out, not_18_out, and_26_out);
  and and_28 (and_28_out, not_12_out, notconnected_3_out[1]);
  and and_29 (and_29_out, and_28_out, not_10_out);
  and and_30 (and_30_out, not_18_out, and_29_out);
  and and_31 (and_31_out, notconnected_3_out[2], not_11_out);
  and and_32 (and_32_out, and_36_out, not_10_out);
  and and_33 (and_33_out, and_31_out, not_10_out);
  and and_34 (and_34_out, not_18_out, and_32_out);
  and and_35 (and_35_out, not_18_out, and_33_out);
  and and_36 (and_36_out, not_12_out, not_11_out);
  not not_11 (not_11_out, notconnected_3_out[1]);
  not not_12 (not_12_out, notconnected_3_out[2]);
  and and_37 (and_37_out, not_13_out, not_14_out);
  not not_13 (not_13_out, notconnected_2_out[5]);
  not not_14 (not_14_out, notconnected_2_out[4]);
  and and_38 (and_38_out, not_14_out, notconnected_2_out[5]);
  not not_15 (not_15_out, notconnected_3_out[0]);
  and and_39 (and_39_out, and_42_out, not_15_out);
  and and_40 (and_40_out, not_18_out, and_39_out);
  and and_41 (and_41_out, not_17_out, notconnected_3_out[1]);
  and and_42 (and_42_out, notconnected_3_out[1], notconnected_3_out[2]);
  and and_43 (and_43_out, and_41_out, not_15_out);
  and and_44 (and_44_out, not_18_out, and_43_out);
  and and_45 (and_45_out, notconnected_3_out[2], not_16_out);
  and and_46 (and_46_out, and_45_out, not_15_out);
  and and_47 (and_47_out, not_18_out, and_46_out);
  and and_48 (and_48_out, not_17_out, not_16_out);
  and and_49 (and_49_out, and_48_out, not_15_out);
  and and_50 (and_50_out, not_18_out, and_49_out);
  not not_16 (not_16_out, notconnected_3_out[1]);
  not not_17 (not_17_out, notconnected_3_out[2]);
  not not_18 (not_18_out, notconnected_2_out[6]);
  // NotConnected on notconnected_2_out
  not not_19 (not_19_out, notconnected_4_out[0]);
  not not_20 (not_20_out, not_19_out);
  and and_51 (and_51_out, and_54_out, not_20_out);
  and and_52 (and_52_out, not_26_out, and_51_out);
  and and_53 (and_53_out, not_22_out, notconnected_4_out[1]);
  and and_54 (and_54_out, notconnected_4_out[1], notconnected_4_out[2]);
  and and_55 (and_55_out, and_53_out, not_20_out);
  and and_56 (and_56_out, not_26_out, and_55_out);
  and and_57 (and_57_out, notconnected_4_out[2], not_21_out);
  and and_58 (and_58_out, and_57_out, not_20_out);
  and and_59 (and_59_out, not_26_out, and_58_out);
  // NotConnected on notconnected_3_out
  and and_60 (and_60_out, not_22_out, not_21_out);
  and and_61 (and_61_out, and_60_out, not_20_out);
  and and_62 (and_62_out, not_26_out, and_61_out);
  not not_21 (not_21_out, notconnected_4_out[1]);
  not not_22 (not_22_out, notconnected_4_out[2]);
  not not_23 (not_23_out, notconnected_4_out[0]);
  and and_63 (and_63_out, notconnected_4_out[1], notconnected_4_out[2]);
  and and_64 (and_64_out, and_69_out, not_23_out);
  and and_65 (and_65_out, and_63_out, not_23_out);
  and and_66 (and_66_out, not_26_out, and_64_out);
  and and_67 (and_67_out, not_26_out, and_65_out);
  and and_68 (and_68_out, notconnected_4_out[2], not_24_out);
  and and_69 (and_69_out, not_25_out, notconnected_4_out[1]);
  and and_70 (and_70_out, and_68_out, not_23_out);
  and and_71 (and_71_out, not_26_out, and_70_out);
  and and_72 (and_72_out, not_25_out, not_24_out);
  and and_73 (and_73_out, and_72_out, not_23_out);
  and and_74 (and_74_out, not_26_out, and_73_out);
  // NotConnected on notconnected_4_out
  not not_24 (not_24_out, notconnected_4_out[1]);
  not not_25 (not_25_out, notconnected_4_out[2]);
  not not_26 (not_26_out, notconnected_2_out[7]);
  // NotConnected on notconnected_5_out
  // NotConnected on notconnected_6_out
  // NotConnected on notconnected_7_out
  ROM #(.AddrBits(8), .Bits(8)) rom_1 (.A(notconnected_7_out), .sel(1'b1), .D(rom_1_d));
  assign driver_1_out[0] = notconnected_2_out[6] ? notconnected_3_out[0] : 1'bz;  // Driver driver_1
  assign driver_1_out[1] = notconnected_2_out[6] ? notconnected_3_out[1] : 1'bz;  // Driver driver_2
  assign driver_3_out[0] = notconnected_2_out[7] ? notconnected_4_out[0] : 1'bz;  // Driver driver_3
  assign driver_3_out[1] = notconnected_2_out[7] ? notconnected_4_out[1] : 1'bz;  // Driver driver_4
  assign driver_1_out[0] = and_30_out ? rom_1_d[0] : 1'bz;  // Driver driver_5
  assign driver_3_out[0] = and_56_out ? rom_1_d[0] : 1'bz;  // Driver driver_6
  assign driver_1_out[2] = notconnected_2_out[6] ? notconnected_3_out[2] : 1'bz;  // Driver driver_7
  assign driver_1_out[3] = notconnected_2_out[6] ? notconnected_3_out[3] : 1'bz;  // Driver driver_8
  assign driver_3_out[2] = notconnected_2_out[7] ? notconnected_4_out[2] : 1'bz;  // Driver driver_9
  assign driver_3_out[3] = notconnected_2_out[7] ? notconnected_4_out[3] : 1'bz;  // Driver driver_10
  assign driver_1_out[1] = and_30_out ? rom_1_d[1] : 1'bz;  // Driver driver_11
  assign driver_1_out[2] = and_30_out ? rom_1_d[2] : 1'bz;  // Driver driver_12
  assign driver_3_out[1] = and_56_out ? rom_1_d[1] : 1'bz;  // Driver driver_13
  assign driver_3_out[2] = and_56_out ? rom_1_d[2] : 1'bz;  // Driver driver_14
  assign driver_1_out[4] = notconnected_2_out[6] ? notconnected_3_out[4] : 1'bz;  // Driver driver_15
  assign driver_1_out[5] = notconnected_2_out[6] ? notconnected_3_out[5] : 1'bz;  // Driver driver_16
  assign driver_3_out[4] = notconnected_2_out[7] ? notconnected_4_out[4] : 1'bz;  // Driver driver_17
  assign driver_3_out[5] = notconnected_2_out[7] ? notconnected_4_out[5] : 1'bz;  // Driver driver_18
  assign driver_1_out[3] = and_30_out ? rom_1_d[3] : 1'bz;  // Driver driver_19
  assign driver_1_out[4] = and_30_out ? rom_1_d[4] : 1'bz;  // Driver driver_20
  assign driver_3_out[3] = and_56_out ? rom_1_d[3] : 1'bz;  // Driver driver_21
  assign driver_3_out[4] = and_56_out ? rom_1_d[4] : 1'bz;  // Driver driver_22
  assign driver_1_out[6] = notconnected_2_out[6] ? notconnected_3_out[6] : 1'bz;  // Driver driver_23
  assign driver_1_out[7] = notconnected_2_out[6] ? notconnected_3_out[7] : 1'bz;  // Driver driver_24
  assign driver_3_out[6] = notconnected_2_out[7] ? notconnected_4_out[6] : 1'bz;  // Driver driver_25
  assign driver_3_out[7] = notconnected_2_out[7] ? notconnected_4_out[7] : 1'bz;  // Driver driver_26
  assign driver_1_out[5] = and_30_out ? rom_1_d[5] : 1'bz;  // Driver driver_27
  assign driver_1_out[6] = and_30_out ? rom_1_d[6] : 1'bz;  // Driver driver_28
  assign driver_3_out[5] = and_56_out ? rom_1_d[5] : 1'bz;  // Driver driver_29
  assign driver_3_out[6] = and_56_out ? rom_1_d[6] : 1'bz;  // Driver driver_30
  assign driver_1_out[7] = and_30_out ? rom_1_d[7] : 1'bz;  // Driver driver_31
  assign driver_3_out[7] = and_56_out ? rom_1_d[7] : 1'bz;  // Driver driver_32
  nand nand_1 (nand_1_out, nand_4_out, nand_2_out);
  nand nand_2 (nand_2_out, nand_1_out, and_24_out);
  nand nand_3 (nand_3_out, nand_2_out, and_24_out, nand_4_out);
  nand nand_4 (nand_4_out, nand_3_out, notconnected_6_out[6]);
  nand nand_5 (nand_5_out, nand_8_out, nand_6_out);
  nand nand_6 (nand_6_out, nand_5_out, and_24_out);
  nand nand_7 (nand_7_out, nand_6_out, and_24_out, nand_8_out);
  nand nand_8 (nand_8_out, nand_7_out, notconnected_6_out[4]);
  nand nand_9 (nand_9_out, nand_12_out, nand_10_out);
  nand nand_10 (nand_10_out, nand_9_out, and_24_out);
  nand nand_11 (nand_11_out, nand_10_out, and_24_out, nand_12_out);
  nand nand_12 (nand_12_out, nand_11_out, notconnected_6_out[2]);
  nand nand_13 (nand_13_out, nand_16_out, nand_14_out);
  nand nand_14 (nand_14_out, nand_13_out, and_24_out);
  nand nand_15 (nand_15_out, nand_14_out, and_24_out, nand_16_out);
  nand nand_16 (nand_16_out, nand_15_out, notconnected_6_out[0]);
  nand nand_17 (nand_17_out, nand_20_out, nand_18_out);
  nand nand_18 (nand_18_out, nand_17_out, and_21_out);
  nand nand_19 (nand_19_out, nand_18_out, and_21_out, nand_20_out);
  nand nand_20 (nand_20_out, nand_19_out, notconnected_6_out[6]);
  nand nand_21 (nand_21_out, nand_24_out, nand_22_out);
  nand nand_22 (nand_22_out, nand_21_out, and_21_out);
  nand nand_23 (nand_23_out, nand_22_out, and_21_out, nand_24_out);
  nand nand_24 (nand_24_out, nand_23_out, notconnected_6_out[4]);
  nand nand_25 (nand_25_out, nand_28_out, nand_26_out);
  nand nand_26 (nand_26_out, nand_25_out, and_21_out);
  nand nand_27 (nand_27_out, nand_26_out, and_21_out, nand_28_out);
  nand nand_28 (nand_28_out, nand_27_out, notconnected_6_out[2]);
  nand nand_29 (nand_29_out, nand_32_out, nand_30_out);
  nand nand_30 (nand_30_out, nand_29_out, and_21_out);
  nand nand_31 (nand_31_out, nand_30_out, and_21_out, nand_32_out);
  nand nand_32 (nand_32_out, nand_31_out, notconnected_6_out[0]);
  nand nand_33 (nand_33_out, nand_36_out, nand_34_out);
  nand nand_34 (nand_34_out, nand_33_out, and_16_out);
  nand nand_35 (nand_35_out, nand_34_out, and_16_out, nand_36_out);
  nand nand_36 (nand_36_out, nand_35_out, notconnected_6_out[6]);
  nand nand_37 (nand_37_out, nand_40_out, nand_38_out);
  nand nand_38 (nand_38_out, nand_37_out, and_16_out);
  nand nand_39 (nand_39_out, nand_38_out, and_16_out, nand_40_out);
  nand nand_40 (nand_40_out, nand_39_out, notconnected_6_out[4]);
  nand nand_41 (nand_41_out, nand_44_out, nand_42_out);
  nand nand_42 (nand_42_out, nand_41_out, and_16_out);
  nand nand_43 (nand_43_out, nand_42_out, and_16_out, nand_44_out);
  nand nand_44 (nand_44_out, nand_43_out, notconnected_6_out[2]);
  nand nand_45 (nand_45_out, nand_48_out, nand_46_out);
  nand nand_46 (nand_46_out, nand_45_out, and_16_out);
  nand nand_47 (nand_47_out, nand_46_out, and_16_out, nand_48_out);
  nand nand_48 (nand_48_out, nand_47_out, notconnected_6_out[0]);
  nand nand_49 (nand_49_out, nand_52_out, nand_50_out);
  nand nand_50 (nand_50_out, nand_49_out, and_17_out);
  nand nand_51 (nand_51_out, nand_50_out, and_17_out, nand_52_out);
  nand nand_52 (nand_52_out, nand_51_out, notconnected_6_out[6]);
  nand nand_53 (nand_53_out, nand_56_out, nand_54_out);
  nand nand_54 (nand_54_out, nand_53_out, and_17_out);
  nand nand_55 (nand_55_out, nand_54_out, and_17_out, nand_56_out);
  nand nand_56 (nand_56_out, nand_55_out, notconnected_6_out[4]);
  nand nand_57 (nand_57_out, nand_60_out, nand_58_out);
  nand nand_58 (nand_58_out, nand_57_out, and_17_out);
  nand nand_59 (nand_59_out, nand_58_out, and_17_out, nand_60_out);
  nand nand_60 (nand_60_out, nand_59_out, notconnected_6_out[2]);
  nand nand_61 (nand_61_out, nand_64_out, nand_62_out);
  nand nand_62 (nand_62_out, nand_61_out, and_17_out);
  nand nand_63 (nand_63_out, nand_62_out, and_17_out, nand_64_out);
  nand nand_64 (nand_64_out, nand_63_out, notconnected_6_out[0]);
  nand nand_65 (nand_65_out, nand_68_out, nand_66_out);
  nand nand_66 (nand_66_out, nand_65_out, and_12_out);
  nand nand_67 (nand_67_out, nand_66_out, and_12_out, nand_68_out);
  nand nand_68 (nand_68_out, nand_67_out, notconnected_6_out[6]);
  nand nand_69 (nand_69_out, nand_72_out, nand_70_out);
  nand nand_70 (nand_70_out, nand_69_out, and_12_out);
  nand nand_71 (nand_71_out, nand_70_out, and_12_out, nand_72_out);
  nand nand_72 (nand_72_out, nand_71_out, notconnected_6_out[4]);
  nand nand_73 (nand_73_out, nand_76_out, nand_74_out);
  nand nand_74 (nand_74_out, nand_73_out, and_12_out);
  nand nand_75 (nand_75_out, nand_74_out, and_12_out, nand_76_out);
  nand nand_76 (nand_76_out, nand_75_out, notconnected_6_out[2]);
  nand nand_77 (nand_77_out, nand_80_out, nand_78_out);
  nand nand_78 (nand_78_out, nand_77_out, and_12_out);
  nand nand_79 (nand_79_out, nand_78_out, and_12_out, nand_80_out);
  nand nand_80 (nand_80_out, nand_79_out, notconnected_6_out[0]);
  nand nand_81 (nand_81_out, nand_84_out, nand_82_out);
  nand nand_82 (nand_82_out, nand_81_out, and_9_out);
  nand nand_83 (nand_83_out, nand_82_out, and_9_out, nand_84_out);
  nand nand_84 (nand_84_out, nand_83_out, notconnected_6_out[6]);
  nand nand_85 (nand_85_out, nand_88_out, nand_86_out);
  nand nand_86 (nand_86_out, nand_85_out, and_9_out);
  nand nand_87 (nand_87_out, nand_86_out, and_9_out, nand_88_out);
  nand nand_88 (nand_88_out, nand_87_out, notconnected_6_out[4]);
  nand nand_89 (nand_89_out, nand_92_out, nand_90_out);
  nand nand_90 (nand_90_out, nand_89_out, and_9_out);
  nand nand_91 (nand_91_out, nand_90_out, and_9_out, nand_92_out);
  nand nand_92 (nand_92_out, nand_91_out, notconnected_6_out[2]);
  nand nand_93 (nand_93_out, nand_96_out, nand_94_out);
  nand nand_94 (nand_94_out, nand_93_out, and_9_out);
  nand nand_95 (nand_95_out, nand_94_out, and_9_out, nand_96_out);
  nand nand_96 (nand_96_out, nand_95_out, notconnected_6_out[0]);
  nand nand_97 (nand_97_out, nand_2_out, nand_98_out);
  nand nand_98 (nand_98_out, nand_97_out, nand_3_out);
  nand nand_99 (nand_99_out, nand_6_out, nand_100_out);
  nand nand_100 (nand_100_out, nand_99_out, nand_7_out);
  nand nand_101 (nand_101_out, nand_10_out, nand_102_out);
  nand nand_102 (nand_102_out, nand_101_out, nand_11_out);
  nand nand_103 (nand_103_out, nand_14_out, nand_104_out);
  nand nand_104 (nand_104_out, nand_103_out, nand_15_out);
  nand nand_105 (nand_105_out, nand_18_out, nand_106_out);
  nand nand_106 (nand_106_out, nand_105_out, nand_19_out);
  nand nand_107 (nand_107_out, nand_22_out, nand_108_out);
  nand nand_108 (nand_108_out, nand_107_out, nand_23_out);
  nand nand_109 (nand_109_out, nand_26_out, nand_110_out);
  nand nand_110 (nand_110_out, nand_109_out, nand_27_out);
  nand nand_111 (nand_111_out, nand_30_out, nand_112_out);
  nand nand_112 (nand_112_out, nand_111_out, nand_31_out);
  nand nand_113 (nand_113_out, nand_34_out, nand_114_out);
  nand nand_114 (nand_114_out, nand_113_out, nand_35_out);
  nand nand_115 (nand_115_out, nand_38_out, nand_116_out);
  nand nand_116 (nand_116_out, nand_115_out, nand_39_out);
  nand nand_117 (nand_117_out, nand_42_out, nand_118_out);
  nand nand_118 (nand_118_out, nand_117_out, nand_43_out);
  nand nand_119 (nand_119_out, nand_46_out, nand_120_out);
  nand nand_120 (nand_120_out, nand_119_out, nand_47_out);
  nand nand_121 (nand_121_out, nand_50_out, nand_122_out);
  nand nand_122 (nand_122_out, nand_121_out, nand_51_out);
  nand nand_123 (nand_123_out, nand_54_out, nand_124_out);
  nand nand_124 (nand_124_out, nand_123_out, nand_55_out);
  nand nand_125 (nand_125_out, nand_58_out, nand_126_out);
  nand nand_126 (nand_126_out, nand_125_out, nand_59_out);
  nand nand_127 (nand_127_out, nand_62_out, nand_128_out);
  nand nand_128 (nand_128_out, nand_127_out, nand_63_out);
  nand nand_129 (nand_129_out, nand_66_out, nand_130_out);
  nand nand_130 (nand_130_out, nand_129_out, nand_67_out);
  nand nand_131 (nand_131_out, nand_70_out, nand_132_out);
  nand nand_132 (nand_132_out, nand_131_out, nand_71_out);
  nand nand_133 (nand_133_out, nand_74_out, nand_134_out);
  nand nand_134 (nand_134_out, nand_133_out, nand_75_out);
  nand nand_135 (nand_135_out, nand_78_out, nand_136_out);
  nand nand_136 (nand_136_out, nand_135_out, nand_79_out);
  nand nand_137 (nand_137_out, nand_82_out, nand_138_out);
  nand nand_138 (nand_138_out, nand_137_out, nand_83_out);
  nand nand_139 (nand_139_out, nand_86_out, nand_140_out);
  nand nand_140 (nand_140_out, nand_139_out, nand_87_out);
  nand nand_141 (nand_141_out, nand_90_out, nand_142_out);
  nand nand_142 (nand_142_out, nand_141_out, nand_91_out);
  nand nand_143 (nand_143_out, nand_94_out, nand_144_out);
  nand nand_144 (nand_144_out, nand_143_out, nand_95_out);
  assign driver_3_out[6] = and_74_out ? nand_97_out : 1'bz;  // Driver driver_33
  assign driver_1_out[6] = and_50_out ? nand_97_out : 1'bz;  // Driver driver_34
  assign driver_3_out[4] = and_74_out ? nand_99_out : 1'bz;  // Driver driver_35
  assign driver_1_out[4] = and_50_out ? nand_99_out : 1'bz;  // Driver driver_36
  assign driver_3_out[2] = and_74_out ? nand_101_out : 1'bz;  // Driver driver_37
  assign driver_1_out[2] = and_50_out ? nand_101_out : 1'bz;  // Driver driver_38
  assign driver_3_out[0] = and_74_out ? nand_103_out : 1'bz;  // Driver driver_39
  assign driver_1_out[0] = and_50_out ? nand_103_out : 1'bz;  // Driver driver_40
  assign driver_3_out[6] = and_71_out ? nand_105_out : 1'bz;  // Driver driver_41
  assign driver_1_out[6] = and_47_out ? nand_105_out : 1'bz;  // Driver driver_42
  assign driver_3_out[4] = and_71_out ? nand_107_out : 1'bz;  // Driver driver_43
  assign driver_1_out[4] = and_47_out ? nand_107_out : 1'bz;  // Driver driver_44
  assign driver_3_out[2] = and_71_out ? nand_109_out : 1'bz;  // Driver driver_45
  assign driver_1_out[2] = and_47_out ? nand_109_out : 1'bz;  // Driver driver_46
  assign driver_3_out[0] = and_71_out ? nand_111_out : 1'bz;  // Driver driver_47
  assign driver_1_out[0] = and_47_out ? nand_111_out : 1'bz;  // Driver driver_48
  assign driver_3_out[6] = and_66_out ? nand_113_out : 1'bz;  // Driver driver_49
  assign driver_1_out[6] = and_44_out ? nand_113_out : 1'bz;  // Driver driver_50
  assign driver_3_out[4] = and_66_out ? nand_115_out : 1'bz;  // Driver driver_51
  assign driver_1_out[4] = and_44_out ? nand_115_out : 1'bz;  // Driver driver_52
  assign driver_3_out[2] = and_66_out ? nand_117_out : 1'bz;  // Driver driver_53
  assign driver_1_out[2] = and_44_out ? nand_117_out : 1'bz;  // Driver driver_54
  assign driver_3_out[0] = and_66_out ? nand_119_out : 1'bz;  // Driver driver_55
  assign driver_1_out[0] = and_44_out ? nand_119_out : 1'bz;  // Driver driver_56
  assign driver_3_out[6] = and_67_out ? nand_121_out : 1'bz;  // Driver driver_57
  assign driver_1_out[6] = and_40_out ? nand_121_out : 1'bz;  // Driver driver_58
  assign driver_3_out[4] = and_67_out ? nand_123_out : 1'bz;  // Driver driver_59
  assign driver_1_out[4] = and_40_out ? nand_123_out : 1'bz;  // Driver driver_60
  assign driver_3_out[2] = and_67_out ? nand_125_out : 1'bz;  // Driver driver_61
  assign driver_1_out[2] = and_40_out ? nand_125_out : 1'bz;  // Driver driver_62
  assign driver_3_out[0] = and_67_out ? nand_127_out : 1'bz;  // Driver driver_63
  assign driver_1_out[0] = and_40_out ? nand_127_out : 1'bz;  // Driver driver_64
  assign driver_3_out[6] = and_62_out ? nand_129_out : 1'bz;  // Driver driver_65
  assign driver_1_out[6] = and_34_out ? nand_129_out : 1'bz;  // Driver driver_66
  assign driver_3_out[4] = and_62_out ? nand_131_out : 1'bz;  // Driver driver_67
  assign driver_1_out[4] = and_34_out ? nand_131_out : 1'bz;  // Driver driver_68
  assign driver_3_out[2] = and_62_out ? nand_133_out : 1'bz;  // Driver driver_69
  assign driver_1_out[2] = and_34_out ? nand_133_out : 1'bz;  // Driver driver_70
  assign driver_3_out[0] = and_62_out ? nand_135_out : 1'bz;  // Driver driver_71
  assign driver_1_out[0] = and_34_out ? nand_135_out : 1'bz;  // Driver driver_72
  assign driver_3_out[6] = and_59_out ? nand_137_out : 1'bz;  // Driver driver_73
  assign driver_1_out[6] = and_35_out ? nand_137_out : 1'bz;  // Driver driver_74
  assign driver_3_out[4] = and_59_out ? nand_139_out : 1'bz;  // Driver driver_75
  assign driver_1_out[4] = and_35_out ? nand_139_out : 1'bz;  // Driver driver_76
  assign driver_3_out[2] = and_59_out ? nand_141_out : 1'bz;  // Driver driver_77
  assign driver_1_out[2] = and_35_out ? nand_141_out : 1'bz;  // Driver driver_78
  assign driver_3_out[0] = and_59_out ? nand_143_out : 1'bz;  // Driver driver_79
  assign driver_1_out[0] = and_35_out ? nand_143_out : 1'bz;  // Driver driver_80
  nand nand_145 (nand_145_out, nand_148_out, nand_146_out);
  nand nand_146 (nand_146_out, nand_145_out, and_24_out);
  nand nand_147 (nand_147_out, nand_146_out, and_24_out, nand_148_out);
  nand nand_148 (nand_148_out, nand_147_out, notconnected_6_out[7]);
  nand nand_149 (nand_149_out, nand_152_out, nand_150_out);
  nand nand_150 (nand_150_out, nand_149_out, and_24_out);
  nand nand_151 (nand_151_out, nand_150_out, and_24_out, nand_152_out);
  nand nand_152 (nand_152_out, nand_151_out, notconnected_6_out[5]);
  nand nand_153 (nand_153_out, nand_156_out, nand_154_out);
  nand nand_154 (nand_154_out, nand_153_out, and_24_out);
  nand nand_155 (nand_155_out, nand_154_out, and_24_out, nand_156_out);
  nand nand_156 (nand_156_out, nand_155_out, notconnected_6_out[3]);
  nand nand_157 (nand_157_out, nand_160_out, nand_158_out);
  nand nand_158 (nand_158_out, nand_157_out, and_24_out);
  nand nand_159 (nand_159_out, nand_158_out, and_24_out, nand_160_out);
  nand nand_160 (nand_160_out, nand_159_out, notconnected_6_out[1]);
  nand nand_161 (nand_161_out, nand_164_out, nand_162_out);
  nand nand_162 (nand_162_out, nand_161_out, and_21_out);
  nand nand_163 (nand_163_out, nand_162_out, and_21_out, nand_164_out);
  nand nand_164 (nand_164_out, nand_163_out, notconnected_6_out[7]);
  nand nand_165 (nand_165_out, nand_168_out, nand_166_out);
  nand nand_166 (nand_166_out, nand_165_out, and_21_out);
  nand nand_167 (nand_167_out, nand_166_out, and_21_out, nand_168_out);
  nand nand_168 (nand_168_out, nand_167_out, notconnected_6_out[5]);
  nand nand_169 (nand_169_out, nand_172_out, nand_170_out);
  nand nand_170 (nand_170_out, nand_169_out, and_21_out);
  nand nand_171 (nand_171_out, nand_170_out, and_21_out, nand_172_out);
  nand nand_172 (nand_172_out, nand_171_out, notconnected_6_out[3]);
  nand nand_173 (nand_173_out, nand_176_out, nand_174_out);
  nand nand_174 (nand_174_out, nand_173_out, and_21_out);
  nand nand_175 (nand_175_out, nand_174_out, and_21_out, nand_176_out);
  nand nand_176 (nand_176_out, nand_175_out, notconnected_6_out[1]);
  nand nand_177 (nand_177_out, nand_180_out, nand_178_out);
  nand nand_178 (nand_178_out, nand_177_out, and_16_out);
  nand nand_179 (nand_179_out, nand_178_out, and_16_out, nand_180_out);
  nand nand_180 (nand_180_out, nand_179_out, notconnected_6_out[7]);
  nand nand_181 (nand_181_out, nand_184_out, nand_182_out);
  nand nand_182 (nand_182_out, nand_181_out, and_16_out);
  nand nand_183 (nand_183_out, nand_182_out, and_16_out, nand_184_out);
  nand nand_184 (nand_184_out, nand_183_out, notconnected_6_out[5]);
  nand nand_185 (nand_185_out, nand_188_out, nand_186_out);
  nand nand_186 (nand_186_out, nand_185_out, and_16_out);
  nand nand_187 (nand_187_out, nand_186_out, and_16_out, nand_188_out);
  nand nand_188 (nand_188_out, nand_187_out, notconnected_6_out[3]);
  nand nand_189 (nand_189_out, nand_192_out, nand_190_out);
  nand nand_190 (nand_190_out, nand_189_out, and_16_out);
  nand nand_191 (nand_191_out, nand_190_out, and_16_out, nand_192_out);
  nand nand_192 (nand_192_out, nand_191_out, notconnected_6_out[1]);
  nand nand_193 (nand_193_out, nand_196_out, nand_194_out);
  nand nand_194 (nand_194_out, nand_193_out, and_17_out);
  nand nand_195 (nand_195_out, nand_194_out, and_17_out, nand_196_out);
  nand nand_196 (nand_196_out, nand_195_out, notconnected_6_out[7]);
  nand nand_197 (nand_197_out, nand_200_out, nand_198_out);
  nand nand_198 (nand_198_out, nand_197_out, and_17_out);
  nand nand_199 (nand_199_out, nand_198_out, and_17_out, nand_200_out);
  nand nand_200 (nand_200_out, nand_199_out, notconnected_6_out[5]);
  nand nand_201 (nand_201_out, nand_204_out, nand_202_out);
  nand nand_202 (nand_202_out, nand_201_out, and_17_out);
  nand nand_203 (nand_203_out, nand_202_out, and_17_out, nand_204_out);
  nand nand_204 (nand_204_out, nand_203_out, notconnected_6_out[3]);
  nand nand_205 (nand_205_out, nand_208_out, nand_206_out);
  nand nand_206 (nand_206_out, nand_205_out, and_17_out);
  nand nand_207 (nand_207_out, nand_206_out, and_17_out, nand_208_out);
  nand nand_208 (nand_208_out, nand_207_out, notconnected_6_out[1]);
  nand nand_209 (nand_209_out, nand_212_out, nand_210_out);
  nand nand_210 (nand_210_out, nand_209_out, and_12_out);
  nand nand_211 (nand_211_out, nand_210_out, and_12_out, nand_212_out);
  nand nand_212 (nand_212_out, nand_211_out, notconnected_6_out[7]);
  nand nand_213 (nand_213_out, nand_216_out, nand_214_out);
  nand nand_214 (nand_214_out, nand_213_out, and_12_out);
  nand nand_215 (nand_215_out, nand_214_out, and_12_out, nand_216_out);
  nand nand_216 (nand_216_out, nand_215_out, notconnected_6_out[5]);
  nand nand_217 (nand_217_out, nand_220_out, nand_218_out);
  nand nand_218 (nand_218_out, nand_217_out, and_12_out);
  nand nand_219 (nand_219_out, nand_218_out, and_12_out, nand_220_out);
  nand nand_220 (nand_220_out, nand_219_out, notconnected_6_out[3]);
  nand nand_221 (nand_221_out, nand_224_out, nand_222_out);
  nand nand_222 (nand_222_out, nand_221_out, and_12_out);
  nand nand_223 (nand_223_out, nand_222_out, and_12_out, nand_224_out);
  nand nand_224 (nand_224_out, nand_223_out, notconnected_6_out[1]);
  nand nand_225 (nand_225_out, nand_228_out, nand_226_out);
  nand nand_226 (nand_226_out, nand_225_out, and_9_out);
  nand nand_227 (nand_227_out, nand_226_out, and_9_out, nand_228_out);
  nand nand_228 (nand_228_out, nand_227_out, notconnected_6_out[7]);
  nand nand_229 (nand_229_out, nand_232_out, nand_230_out);
  nand nand_230 (nand_230_out, nand_229_out, and_9_out);
  nand nand_231 (nand_231_out, nand_230_out, and_9_out, nand_232_out);
  nand nand_232 (nand_232_out, nand_231_out, notconnected_6_out[5]);
  nand nand_233 (nand_233_out, nand_236_out, nand_234_out);
  nand nand_234 (nand_234_out, nand_233_out, and_9_out);
  nand nand_235 (nand_235_out, nand_234_out, and_9_out, nand_236_out);
  nand nand_236 (nand_236_out, nand_235_out, notconnected_6_out[3]);
  nand nand_237 (nand_237_out, nand_240_out, nand_238_out);
  nand nand_238 (nand_238_out, nand_237_out, and_9_out);
  nand nand_239 (nand_239_out, nand_238_out, and_9_out, nand_240_out);
  nand nand_240 (nand_240_out, nand_239_out, notconnected_6_out[1]);
  nand nand_241 (nand_241_out, nand_146_out, nand_242_out);
  nand nand_242 (nand_242_out, nand_241_out, nand_147_out);
  nand nand_243 (nand_243_out, nand_150_out, nand_244_out);
  nand nand_244 (nand_244_out, nand_243_out, nand_151_out);
  nand nand_245 (nand_245_out, nand_154_out, nand_246_out);
  nand nand_246 (nand_246_out, nand_245_out, nand_155_out);
  nand nand_247 (nand_247_out, nand_158_out, nand_248_out);
  nand nand_248 (nand_248_out, nand_247_out, nand_159_out);
  nand nand_249 (nand_249_out, nand_162_out, nand_250_out);
  nand nand_250 (nand_250_out, nand_249_out, nand_163_out);
  nand nand_251 (nand_251_out, nand_166_out, nand_252_out);
  nand nand_252 (nand_252_out, nand_251_out, nand_167_out);
  nand nand_253 (nand_253_out, nand_170_out, nand_254_out);
  nand nand_254 (nand_254_out, nand_253_out, nand_171_out);
  nand nand_255 (nand_255_out, nand_174_out, nand_256_out);
  nand nand_256 (nand_256_out, nand_255_out, nand_175_out);
  nand nand_257 (nand_257_out, nand_178_out, nand_258_out);
  nand nand_258 (nand_258_out, nand_257_out, nand_179_out);
  nand nand_259 (nand_259_out, nand_182_out, nand_260_out);
  nand nand_260 (nand_260_out, nand_259_out, nand_183_out);
  nand nand_261 (nand_261_out, nand_186_out, nand_262_out);
  nand nand_262 (nand_262_out, nand_261_out, nand_187_out);
  nand nand_263 (nand_263_out, nand_190_out, nand_264_out);
  nand nand_264 (nand_264_out, nand_263_out, nand_191_out);
  nand nand_265 (nand_265_out, nand_194_out, nand_266_out);
  nand nand_266 (nand_266_out, nand_265_out, nand_195_out);
  nand nand_267 (nand_267_out, nand_198_out, nand_268_out);
  nand nand_268 (nand_268_out, nand_267_out, nand_199_out);
  nand nand_269 (nand_269_out, nand_202_out, nand_270_out);
  nand nand_270 (nand_270_out, nand_269_out, nand_203_out);
  nand nand_271 (nand_271_out, nand_206_out, nand_272_out);
  nand nand_272 (nand_272_out, nand_271_out, nand_207_out);
  nand nand_273 (nand_273_out, nand_210_out, nand_274_out);
  nand nand_274 (nand_274_out, nand_273_out, nand_211_out);
  nand nand_275 (nand_275_out, nand_214_out, nand_276_out);
  nand nand_276 (nand_276_out, nand_275_out, nand_215_out);
  nand nand_277 (nand_277_out, nand_218_out, nand_278_out);
  nand nand_278 (nand_278_out, nand_277_out, nand_219_out);
  nand nand_279 (nand_279_out, nand_222_out, nand_280_out);
  nand nand_280 (nand_280_out, nand_279_out, nand_223_out);
  nand nand_281 (nand_281_out, nand_226_out, nand_282_out);
  nand nand_282 (nand_282_out, nand_281_out, nand_227_out);
  nand nand_283 (nand_283_out, nand_230_out, nand_284_out);
  nand nand_284 (nand_284_out, nand_283_out, nand_231_out);
  nand nand_285 (nand_285_out, nand_234_out, nand_286_out);
  nand nand_286 (nand_286_out, nand_285_out, nand_235_out);
  nand nand_287 (nand_287_out, nand_238_out, nand_288_out);
  nand nand_288 (nand_288_out, nand_287_out, nand_239_out);
  assign driver_3_out[7] = and_74_out ? nand_241_out : 1'bz;  // Driver driver_81
  assign driver_1_out[7] = and_50_out ? nand_241_out : 1'bz;  // Driver driver_82
  assign driver_3_out[5] = and_74_out ? nand_243_out : 1'bz;  // Driver driver_83
  assign driver_1_out[5] = and_50_out ? nand_243_out : 1'bz;  // Driver driver_84
  assign driver_3_out[3] = and_74_out ? nand_245_out : 1'bz;  // Driver driver_85
  assign driver_1_out[3] = and_50_out ? nand_245_out : 1'bz;  // Driver driver_86
  assign driver_3_out[1] = and_74_out ? nand_247_out : 1'bz;  // Driver driver_87
  assign driver_1_out[1] = and_50_out ? nand_247_out : 1'bz;  // Driver driver_88
  assign driver_3_out[7] = and_71_out ? nand_249_out : 1'bz;  // Driver driver_89
  assign driver_1_out[7] = and_47_out ? nand_249_out : 1'bz;  // Driver driver_90
  assign driver_3_out[5] = and_71_out ? nand_251_out : 1'bz;  // Driver driver_91
  assign driver_1_out[5] = and_47_out ? nand_251_out : 1'bz;  // Driver driver_92
  assign driver_3_out[3] = and_71_out ? nand_253_out : 1'bz;  // Driver driver_93
  assign driver_1_out[3] = and_47_out ? nand_253_out : 1'bz;  // Driver driver_94
  assign driver_3_out[1] = and_71_out ? nand_255_out : 1'bz;  // Driver driver_95
  assign driver_1_out[1] = and_47_out ? nand_255_out : 1'bz;  // Driver driver_96
  assign driver_3_out[7] = and_66_out ? nand_257_out : 1'bz;  // Driver driver_97
  assign driver_1_out[7] = and_44_out ? nand_257_out : 1'bz;  // Driver driver_98
  assign driver_3_out[5] = and_66_out ? nand_259_out : 1'bz;  // Driver driver_99
  assign driver_1_out[5] = and_44_out ? nand_259_out : 1'bz;  // Driver driver_100
  assign driver_3_out[3] = and_66_out ? nand_261_out : 1'bz;  // Driver driver_101
  assign driver_1_out[3] = and_44_out ? nand_261_out : 1'bz;  // Driver driver_102
  assign driver_3_out[1] = and_66_out ? nand_263_out : 1'bz;  // Driver driver_103
  assign driver_1_out[1] = and_44_out ? nand_263_out : 1'bz;  // Driver driver_104
  assign driver_3_out[7] = and_67_out ? nand_265_out : 1'bz;  // Driver driver_105
  assign driver_1_out[7] = and_40_out ? nand_265_out : 1'bz;  // Driver driver_106
  assign driver_3_out[5] = and_67_out ? nand_267_out : 1'bz;  // Driver driver_107
  assign driver_1_out[5] = and_40_out ? nand_267_out : 1'bz;  // Driver driver_108
  assign driver_3_out[3] = and_67_out ? nand_269_out : 1'bz;  // Driver driver_109
  assign driver_1_out[3] = and_40_out ? nand_269_out : 1'bz;  // Driver driver_110
  assign driver_3_out[1] = and_67_out ? nand_271_out : 1'bz;  // Driver driver_111
  assign driver_1_out[1] = and_40_out ? nand_271_out : 1'bz;  // Driver driver_112
  assign driver_3_out[7] = and_62_out ? nand_273_out : 1'bz;  // Driver driver_113
  assign driver_1_out[7] = and_34_out ? nand_273_out : 1'bz;  // Driver driver_114
  assign driver_3_out[5] = and_62_out ? nand_275_out : 1'bz;  // Driver driver_115
  assign driver_1_out[5] = and_34_out ? nand_275_out : 1'bz;  // Driver driver_116
  assign driver_3_out[3] = and_62_out ? nand_277_out : 1'bz;  // Driver driver_117
  assign driver_1_out[3] = and_34_out ? nand_277_out : 1'bz;  // Driver driver_118
  assign driver_3_out[1] = and_62_out ? nand_279_out : 1'bz;  // Driver driver_119
  assign driver_1_out[1] = and_34_out ? nand_279_out : 1'bz;  // Driver driver_120
  assign driver_3_out[7] = and_59_out ? nand_281_out : 1'bz;  // Driver driver_121
  assign driver_1_out[7] = and_35_out ? nand_281_out : 1'bz;  // Driver driver_122
  assign driver_3_out[5] = and_59_out ? nand_283_out : 1'bz;  // Driver driver_123
  assign driver_1_out[5] = and_35_out ? nand_283_out : 1'bz;  // Driver driver_124
  assign driver_3_out[3] = and_59_out ? nand_285_out : 1'bz;  // Driver driver_125
  assign driver_1_out[3] = and_35_out ? nand_285_out : 1'bz;  // Driver driver_126
  assign driver_3_out[1] = and_59_out ? nand_287_out : 1'bz;  // Driver driver_127
  assign driver_1_out[1] = and_35_out ? nand_287_out : 1'bz;  // Driver driver_128
  xor xor_1 (xor_1_out, driver_1_out[7], and_108_out);
  xor xor_2 (xor_2_out, driver_1_out[6], and_108_out);
  xor xor_3 (xor_3_out, driver_1_out[5], and_108_out);
  xor xor_4 (xor_4_out, driver_1_out[4], and_108_out);
  xor xor_5 (xor_5_out, driver_1_out[3], and_108_out);
  xor xor_6 (xor_6_out, driver_1_out[2], and_108_out);
  xor xor_7 (xor_7_out, driver_1_out[1], and_108_out);
  xor xor_8 (xor_8_out, driver_1_out[0], and_108_out);
  and and_75 (and_90_out[0], driver_1_out[0], driver_3_out[0]);
  and and_76 (and_90_out[1], driver_1_out[1], driver_3_out[1]);
  nand nand_289 (nand_296_out[0], driver_1_out[0], driver_3_out[0]);
  nand nand_290 (nand_296_out[1], driver_1_out[1], driver_3_out[1]);
  or or_1 (or_16_out[0], driver_1_out[0], driver_3_out[0]);
  or or_2 (or_16_out[1], driver_1_out[1], driver_3_out[1]);
  nor nor_1 (nor_8_out[0], driver_1_out[0], driver_3_out[0]);
  nor nor_2 (nor_8_out[1], driver_1_out[1], driver_3_out[1]);
  xor xor_9 (xor_24_out[0], driver_1_out[0], driver_3_out[0]);
  xor xor_10 (xor_24_out[1], driver_1_out[1], driver_3_out[1]);
  and and_77 (and_90_out[2], driver_1_out[2], driver_3_out[2]);
  nand nand_291 (nand_296_out[2], driver_1_out[2], driver_3_out[2]);
  or or_3 (or_16_out[2], driver_1_out[2], driver_3_out[2]);
  nor nor_3 (nor_8_out[2], driver_1_out[2], driver_3_out[2]);
  xor xor_11 (xor_24_out[2], driver_1_out[2], driver_3_out[2]);
  and and_78 (and_90_out[3], driver_1_out[3], driver_3_out[3]);
  nand nand_292 (nand_296_out[3], driver_1_out[3], driver_3_out[3]);
  or or_4 (or_16_out[3], driver_1_out[3], driver_3_out[3]);
  nor nor_4 (nor_8_out[3], driver_1_out[3], driver_3_out[3]);
  xor xor_12 (xor_24_out[3], driver_1_out[3], driver_3_out[3]);
  and and_79 (and_90_out[4], driver_1_out[4], driver_3_out[4]);
  and and_80 (and_90_out[5], driver_1_out[5], driver_3_out[5]);
  nand nand_293 (nand_296_out[4], driver_1_out[4], driver_3_out[4]);
  nand nand_294 (nand_296_out[5], driver_1_out[5], driver_3_out[5]);
  or or_5 (or_16_out[4], driver_1_out[4], driver_3_out[4]);
  or or_6 (or_16_out[5], driver_1_out[5], driver_3_out[5]);
  nor nor_5 (nor_8_out[4], driver_1_out[4], driver_3_out[4]);
  nor nor_6 (nor_8_out[5], driver_1_out[5], driver_3_out[5]);
  xor xor_13 (xor_24_out[4], driver_1_out[4], driver_3_out[4]);
  xor xor_14 (xor_24_out[5], driver_1_out[5], driver_3_out[5]);
  and and_81 (and_81_out, xor_1_out, driver_3_out[7]);
  xor xor_15 (xor_15_out, driver_3_out[7], xor_1_out);
  and and_82 (and_82_out, xor_2_out, driver_3_out[6]);
  xor xor_16 (xor_16_out, driver_3_out[6], xor_2_out);
  and and_83 (and_83_out, xor_3_out, driver_3_out[5]);
  xor xor_17 (xor_17_out, driver_3_out[5], xor_3_out);
  and and_84 (and_84_out, xor_4_out, driver_3_out[4]);
  xor xor_18 (xor_18_out, driver_3_out[4], xor_4_out);
  and and_85 (and_85_out, xor_5_out, driver_3_out[3]);
  xor xor_19 (xor_19_out, driver_3_out[3], xor_5_out);
  and and_86 (and_86_out, xor_6_out, driver_3_out[2]);
  xor xor_20 (xor_20_out, driver_3_out[2], xor_6_out);
  and and_87 (and_87_out, xor_7_out, driver_3_out[1]);
  xor xor_21 (xor_21_out, driver_3_out[1], xor_7_out);
  and and_88 (and_88_out, xor_8_out, driver_3_out[0]);
  xor xor_22 (xor_22_out, driver_3_out[0], xor_8_out);
  and and_89 (and_90_out[6], driver_1_out[6], driver_3_out[6]);
  nand nand_295 (nand_296_out[6], driver_1_out[6], driver_3_out[6]);
  or or_7 (or_16_out[6], driver_1_out[6], driver_3_out[6]);
  nor nor_7 (nor_8_out[6], driver_1_out[6], driver_3_out[6]);
  xor xor_23 (xor_24_out[6], driver_1_out[6], driver_3_out[6]);
  or or_8 (or_8_out, and_81_out, and_91_out);
  or or_9 (or_9_out, and_82_out, and_92_out);
  or or_10 (or_10_out, and_83_out, and_93_out);
  or or_11 (or_11_out, and_84_out, and_94_out);
  or or_12 (or_12_out, and_85_out, and_95_out);
  or or_13 (or_13_out, and_86_out, and_96_out);
  or or_14 (or_14_out, and_87_out, and_97_out);
  or or_15 (or_15_out, and_88_out, and_98_out);
  and and_90 (and_90_out[7], driver_1_out[7], driver_3_out[7]);
  nand nand_296 (nand_296_out[7], driver_1_out[7], driver_3_out[7]);
  or or_16 (or_16_out[7], driver_1_out[7], driver_3_out[7]);
  nor nor_8 (nor_8_out[7], driver_1_out[7], driver_3_out[7]);
  xor xor_24 (xor_24_out[7], driver_1_out[7], driver_3_out[7]);
  and and_91 (and_91_out, xor_15_out, or_9_out);
  xor xor_25 (xor_32_out[7], xor_15_out, or_9_out);
  and and_92 (and_92_out, xor_16_out, or_10_out);
  xor xor_26 (xor_32_out[6], xor_16_out, or_10_out);
  and and_93 (and_93_out, xor_17_out, or_11_out);
  xor xor_27 (xor_32_out[5], xor_17_out, or_11_out);
  and and_94 (and_94_out, xor_18_out, or_12_out);
  xor xor_28 (xor_32_out[4], xor_18_out, or_12_out);
  and and_95 (and_95_out, xor_19_out, or_13_out);
  xor xor_29 (xor_32_out[3], xor_19_out, or_13_out);
  and and_96 (and_96_out, xor_20_out, or_14_out);
  xor xor_30 (xor_32_out[2], xor_20_out, or_14_out);
  and and_97 (and_97_out, xor_21_out, or_15_out);
  xor xor_31 (xor_32_out[1], xor_21_out, or_15_out);
  and and_98 (and_98_out, xor_22_out, and_108_out);
  xor xor_32 (xor_32_out[0], xor_22_out, and_108_out);
  assign driver_160_out[0] = and_109_out ? and_90_out[0] : 1'bz;  // Driver driver_129
  assign driver_160_out[1] = and_109_out ? and_90_out[1] : 1'bz;  // Driver driver_130
  assign driver_160_out[0] = and_110_out ? nand_296_out[0] : 1'bz;  // Driver driver_131
  assign driver_160_out[1] = and_110_out ? nand_296_out[1] : 1'bz;  // Driver driver_132
  assign driver_160_out[0] = and_111_out ? or_16_out[0] : 1'bz;  // Driver driver_133
  assign driver_160_out[1] = and_111_out ? or_16_out[1] : 1'bz;  // Driver driver_134
  assign driver_160_out[0] = and_112_out ? nor_8_out[0] : 1'bz;  // Driver driver_135
  assign driver_160_out[1] = and_112_out ? nor_8_out[1] : 1'bz;  // Driver driver_136
  assign driver_160_out[0] = and_113_out ? xor_24_out[0] : 1'bz;  // Driver driver_137
  assign driver_160_out[1] = and_113_out ? xor_24_out[1] : 1'bz;  // Driver driver_138
  assign driver_160_out[2] = and_109_out ? and_90_out[2] : 1'bz;  // Driver driver_139
  assign driver_160_out[3] = and_109_out ? and_90_out[3] : 1'bz;  // Driver driver_140
  assign driver_160_out[2] = and_110_out ? nand_296_out[2] : 1'bz;  // Driver driver_141
  assign driver_160_out[3] = and_110_out ? nand_296_out[3] : 1'bz;  // Driver driver_142
  assign driver_160_out[2] = and_111_out ? or_16_out[2] : 1'bz;  // Driver driver_143
  assign driver_160_out[3] = and_111_out ? or_16_out[3] : 1'bz;  // Driver driver_144
  assign driver_160_out[2] = and_112_out ? nor_8_out[2] : 1'bz;  // Driver driver_145
  assign driver_160_out[3] = and_112_out ? nor_8_out[3] : 1'bz;  // Driver driver_146
  assign driver_160_out[2] = and_113_out ? xor_24_out[2] : 1'bz;  // Driver driver_147
  assign driver_160_out[3] = and_113_out ? xor_24_out[3] : 1'bz;  // Driver driver_148
  assign driver_160_out[4] = and_109_out ? and_90_out[4] : 1'bz;  // Driver driver_149
  assign driver_160_out[5] = and_109_out ? and_90_out[5] : 1'bz;  // Driver driver_150
  assign driver_160_out[4] = and_110_out ? nand_296_out[4] : 1'bz;  // Driver driver_151
  assign driver_160_out[5] = and_110_out ? nand_296_out[5] : 1'bz;  // Driver driver_152
  assign driver_160_out[4] = and_111_out ? or_16_out[4] : 1'bz;  // Driver driver_153
  assign driver_160_out[5] = and_111_out ? or_16_out[5] : 1'bz;  // Driver driver_154
  assign driver_160_out[4] = and_112_out ? nor_8_out[4] : 1'bz;  // Driver driver_155
  assign driver_160_out[5] = and_112_out ? nor_8_out[5] : 1'bz;  // Driver driver_156
  assign driver_160_out[4] = and_113_out ? xor_24_out[4] : 1'bz;  // Driver driver_157
  assign driver_160_out[5] = and_113_out ? xor_24_out[5] : 1'bz;  // Driver driver_158
  assign driver_160_out[6] = and_109_out ? and_90_out[6] : 1'bz;  // Driver driver_159
  assign driver_160_out[7] = and_109_out ? and_90_out[7] : 1'bz;  // Driver driver_160
  assign driver_160_out[6] = and_110_out ? nand_296_out[6] : 1'bz;  // Driver driver_161
  assign driver_160_out[7] = and_110_out ? nand_296_out[7] : 1'bz;  // Driver driver_162
  assign driver_160_out[6] = and_111_out ? or_16_out[6] : 1'bz;  // Driver driver_163
  assign driver_160_out[7] = and_111_out ? or_16_out[7] : 1'bz;  // Driver driver_164
  assign driver_160_out[6] = and_112_out ? nor_8_out[6] : 1'bz;  // Driver driver_165
  assign driver_160_out[7] = and_112_out ? nor_8_out[7] : 1'bz;  // Driver driver_166
  assign driver_160_out[6] = and_113_out ? xor_24_out[6] : 1'bz;  // Driver driver_167
  assign driver_160_out[7] = and_113_out ? xor_24_out[7] : 1'bz;  // Driver driver_168
  DipSwitch dipswitch_1 (.out(dipswitch_1_out));
  not not_27 (not_27_out, C_5);
  assign driver_160_out[0] = or_25_out ? xor_32_out[0] : 1'bz;  // Driver driver_169
  not not_28 (not_28_out, C_4);
  not not_29 (not_29_out, C_4);
  assign driver_160_out[1] = or_25_out ? xor_32_out[1] : 1'bz;  // Driver driver_170
  assign driver_160_out[2] = or_25_out ? xor_32_out[2] : 1'bz;  // Driver driver_171
  not not_30 (not_30_out, C_3);
  and and_99 (and_99_out, not_30_out, not_28_out);
  and and_100 (and_100_out, C_3, not_28_out);
  and and_101 (and_101_out, not_30_out, C_4);
  and and_102 (and_102_out, C_4, C_3);
  not not_31 (not_31_out, C_5);
  not not_32 (not_32_out, C_3);
  and and_103 (and_103_out, not_32_out, not_29_out);
  and and_104 (and_104_out, C_3, not_29_out);
  and and_105 (and_105_out, not_32_out, C_4);
  and and_106 (and_106_out, C_4, C_3);
  not not_33 (not_33_out, not_27_out);
  assign driver_160_out[3] = or_25_out ? xor_32_out[3] : 1'bz;  // Driver driver_172
  assign driver_160_out[4] = or_25_out ? xor_32_out[4] : 1'bz;  // Driver driver_173
  assign driver_160_out[5] = or_25_out ? xor_32_out[5] : 1'bz;  // Driver driver_174
  assign driver_160_out[6] = or_25_out ? xor_32_out[6] : 1'bz;  // Driver driver_175
  and and_107 (and_107_out, and_99_out, not_31_out);
  and and_108 (and_108_out, and_100_out, not_31_out);
  and and_109 (and_109_out, and_101_out, not_31_out);
  and and_110 (and_110_out, and_102_out, not_31_out);
  and and_111 (and_111_out, and_103_out, not_33_out);
  and and_112 (and_112_out, and_104_out, not_33_out);
  and and_113 (and_113_out, and_105_out, not_33_out);
  // And and_114 has open pins: In_1=and_106_out, In_2=not_33_out, out=open
  assign driver_160_out[7] = or_25_out ? xor_32_out[7] : 1'bz;  // Driver driver_176
  and and_115 (and_138_out[0], dipswitch_1_out, 1'b0);
  and and_116 (and_116_out, 1'b0, nand_343_out[7]);
  xor xor_33 (xor_33_out, nand_343_out[7], 1'b0);
  and and_117 (and_117_out, 1'b0, nand_343_out[6]);
  xor xor_34 (xor_34_out, nand_343_out[6], 1'b0);
  and and_118 (and_118_out, 1'b0, nand_343_out[5]);
  xor xor_35 (xor_35_out, nand_343_out[5], 1'b0);
  and and_119 (and_119_out, 1'b0, nand_343_out[4]);
  xor xor_36 (xor_36_out, nand_343_out[4], 1'b0);
  and and_120 (and_120_out, 1'b0, nand_343_out[3]);
  xor xor_37 (xor_37_out, nand_343_out[3], 1'b0);
  and and_121 (and_121_out, 1'b0, nand_343_out[2]);
  xor xor_38 (xor_38_out, nand_343_out[2], 1'b0);
  and and_122 (and_122_out, 1'b0, nand_343_out[1]);
  xor xor_39 (xor_39_out, nand_343_out[1], 1'b0);
  and and_123 (and_123_out, 1'b1, nand_343_out[0]);
  xor xor_40 (xor_40_out, nand_343_out[0], 1'b1);
  and and_124 (and_138_out[1], dipswitch_1_out, 1'b0);
  and and_125 (and_138_out[2], dipswitch_1_out, 1'b0);
  // Or or_17 has open pins: In_1=and_116_out, In_2=and_126_out, out=open
  and and_126 (and_126_out, xor_33_out, or_18_out);
  xor xor_41 (xor_48_out[7], xor_33_out, or_18_out);
  or or_18 (or_18_out, and_117_out, and_127_out);
  and and_127 (and_127_out, xor_34_out, or_19_out);
  xor xor_42 (xor_48_out[6], xor_34_out, or_19_out);
  or or_19 (or_19_out, and_118_out, and_128_out);
  and and_128 (and_128_out, xor_35_out, or_20_out);
  xor xor_43 (xor_48_out[5], xor_35_out, or_20_out);
  or or_20 (or_20_out, and_119_out, and_129_out);
  and and_129 (and_129_out, xor_36_out, or_21_out);
  xor xor_44 (xor_48_out[4], xor_36_out, or_21_out);
  or or_21 (or_21_out, and_120_out, and_131_out);
  or or_22 (or_22_out, and_121_out, and_132_out);
  or or_23 (or_23_out, and_122_out, and_133_out);
  or or_24 (or_24_out, and_123_out, and_134_out);
  // NotConnected on notconnected_8_out
  and and_130 (and_138_out[3], dipswitch_1_out, 1'b0);
  and and_131 (and_131_out, xor_37_out, or_22_out);
  xor xor_45 (xor_48_out[3], xor_37_out, or_22_out);
  and and_132 (and_132_out, xor_38_out, or_23_out);
  xor xor_46 (xor_48_out[2], xor_38_out, or_23_out);
  and and_133 (and_133_out, xor_39_out, or_24_out);
  xor xor_47 (xor_48_out[1], xor_39_out, or_24_out);
  and and_134 (and_134_out, xor_40_out, notconnected_8_out);
  xor xor_48 (xor_48_out[0], xor_40_out, notconnected_8_out);
  or or_25 (or_25_out, and_107_out, and_108_out);
  and and_135 (and_138_out[4], dipswitch_1_out, 1'b0);
  and and_136 (and_138_out[5], dipswitch_1_out, 1'b0);
  and and_137 (and_138_out[6], dipswitch_1_out, 1'b0);
  not not_34 (not_34_out, dipswitch_1_out);
  and and_138 (and_138_out[7], dipswitch_1_out, 1'b0);
  or or_26 (or_33_out[0], and_146_out[0], and_138_out[0]);
  or or_27 (or_33_out[1], and_146_out[1], and_138_out[1]);
  or or_28 (or_33_out[2], and_146_out[2], and_138_out[2]);
  and and_139 (and_146_out[0], not_34_out, xor_48_out[0]);
  and and_140 (and_146_out[1], not_34_out, xor_48_out[1]);
  and and_141 (and_146_out[2], not_34_out, xor_48_out[2]);
  and and_142 (and_146_out[3], not_34_out, xor_48_out[3]);
  and and_143 (and_146_out[4], not_34_out, xor_48_out[4]);
  and and_144 (and_146_out[5], not_34_out, xor_48_out[5]);
  and and_145 (and_146_out[6], not_34_out, xor_48_out[6]);
  and and_146 (and_146_out[7], not_34_out, xor_48_out[7]);
  or or_29 (or_33_out[3], and_146_out[3], and_138_out[3]);
  or or_30 (or_33_out[4], and_146_out[4], and_138_out[4]);
  or or_31 (or_33_out[5], and_146_out[5], and_138_out[5]);
  or or_32 (or_33_out[6], and_146_out[6], and_138_out[6]);
  assign notconnected_6_out[0] = and_37_out ? driver_160_out[0] : 1'bz;  // Driver driver_177
  or or_33 (or_33_out[7], and_146_out[7], and_138_out[7]);
  assign notconnected_6_out[1] = and_37_out ? driver_160_out[1] : 1'bz;  // Driver driver_178
  assign notconnected_6_out[2] = and_37_out ? driver_160_out[2] : 1'bz;  // Driver driver_179
  assign notconnected_6_out[3] = and_37_out ? driver_160_out[3] : 1'bz;  // Driver driver_180
  assign notconnected_6_out[4] = and_37_out ? driver_160_out[4] : 1'bz;  // Driver driver_181
  assign notconnected_6_out[5] = and_37_out ? driver_160_out[5] : 1'bz;  // Driver driver_182
  assign notconnected_6_out[6] = and_37_out ? driver_160_out[6] : 1'bz;  // Driver driver_183
  assign notconnected_6_out[7] = and_37_out ? driver_160_out[7] : 1'bz;  // Driver driver_184
  nand nand_297 (nand_297_out, nand_300_out, nand_298_out);
  nand nand_298 (nand_298_out, nand_297_out, clk);
  nand nand_299 (nand_299_out, nand_298_out, clk, nand_300_out);
  nand nand_300 (nand_300_out, nand_299_out, or_33_out[6]);
  nand nand_301 (nand_301_out, nand_304_out, nand_302_out);
  nand nand_302 (nand_302_out, nand_301_out, clk);
  nand nand_303 (nand_303_out, nand_302_out, clk, nand_304_out);
  nand nand_304 (nand_304_out, nand_303_out, or_33_out[4]);
  nand nand_305 (nand_305_out, nand_308_out, nand_306_out);
  nand nand_306 (nand_306_out, nand_305_out, clk);
  nand nand_307 (nand_307_out, nand_306_out, clk, nand_308_out);
  nand nand_308 (nand_308_out, nand_307_out, or_33_out[2]);
  nand nand_309 (nand_309_out, nand_312_out, nand_310_out);
  nand nand_310 (nand_310_out, nand_309_out, clk);
  nand nand_311 (nand_311_out, nand_310_out, clk, nand_312_out);
  nand nand_312 (nand_312_out, nand_311_out, or_33_out[0]);
  nand nand_313 (nand_343_out[6], nand_298_out, nand_314_out);
  nand nand_314 (nand_314_out, nand_343_out[6], nand_299_out);
  nand nand_315 (nand_343_out[4], nand_302_out, nand_316_out);
  nand nand_316 (nand_316_out, nand_343_out[4], nand_303_out);
  nand nand_317 (nand_343_out[2], nand_306_out, nand_318_out);
  nand nand_318 (nand_318_out, nand_343_out[2], nand_307_out);
  nand nand_319 (nand_343_out[0], nand_310_out, nand_320_out);
  nand nand_320 (nand_320_out, nand_343_out[0], nand_311_out);
  and and_147 (and_147_out, nand_343_out[6], 1'b0);
  and and_148 (and_148_out, nand_343_out[4], 1'b0);
  and and_149 (and_149_out, nand_343_out[2], 1'b0);
  and and_150 (and_150_out, nand_343_out[0], 1'b0);
  nand nand_321 (nand_321_out, nand_324_out, nand_322_out);
  nand nand_322 (nand_322_out, nand_321_out, clk);
  nand nand_323 (nand_323_out, nand_322_out, clk, nand_324_out);
  nand nand_324 (nand_324_out, nand_323_out, or_33_out[7]);
  nand nand_325 (nand_325_out, nand_328_out, nand_326_out);
  nand nand_326 (nand_326_out, nand_325_out, clk);
  nand nand_327 (nand_327_out, nand_326_out, clk, nand_328_out);
  nand nand_328 (nand_328_out, nand_327_out, or_33_out[5]);
  nand nand_329 (nand_329_out, nand_332_out, nand_330_out);
  nand nand_330 (nand_330_out, nand_329_out, clk);
  nand nand_331 (nand_331_out, nand_330_out, clk, nand_332_out);
  nand nand_332 (nand_332_out, nand_331_out, or_33_out[3]);
  nand nand_333 (nand_333_out, nand_336_out, nand_334_out);
  nand nand_334 (nand_334_out, nand_333_out, clk);
  nand nand_335 (nand_335_out, nand_334_out, clk, nand_336_out);
  nand nand_336 (nand_336_out, nand_335_out, or_33_out[1]);
  nand nand_337 (nand_343_out[7], nand_322_out, nand_338_out);
  nand nand_338 (nand_338_out, nand_343_out[7], nand_323_out);
  and and_151 (and_151_out, nand_343_out[7], 1'b0);
  nand nand_339 (nand_343_out[5], nand_326_out, nand_340_out);
  nand nand_340 (nand_340_out, nand_343_out[5], nand_327_out);
  and and_152 (and_152_out, nand_343_out[5], 1'b0);
  nand nand_341 (nand_343_out[3], nand_330_out, nand_342_out);
  nand nand_342 (nand_342_out, nand_343_out[3], nand_331_out);
  and and_153 (and_153_out, nand_343_out[3], 1'b0);
  nand nand_343 (nand_343_out[1], nand_334_out, nand_344_out);
  nand nand_344 (nand_344_out, nand_343_out[1], nand_335_out);
  and and_154 (and_154_out, nand_343_out[1], 1'b0);
  not not_35 (not_35_out, In_3);
  not not_36 (not_36_out, In_2);
  not not_37 (not_37_out, In_1);
  not not_38 (not_38_out, In_3);
  not not_39 (not_39_out, In_2);
  not not_40 (not_40_out, In_1);
  not not_41 (not_41_out, not_35_out);
  and and_155 (and_155_out, not_37_out, not_36_out);
  and and_156 (and_156_out, In_1, not_36_out);
  and and_157 (and_157_out, not_37_out, In_2);
  and and_158 (and_158_out, In_2, In_1);
  and and_159 (and_159_out, not_40_out, not_39_out);
  and and_160 (and_160_out, In_1, not_39_out);
  and and_161 (and_161_out, not_40_out, In_2);
  and and_162 (and_162_out, In_2, In_1);
  and and_163 (and_163_out, and_155_out, not_38_out);
  and and_164 (and_164_out, and_156_out, not_38_out);
  and and_165 (and_165_out, and_157_out, not_38_out);
  and and_166 (and_166_out, and_158_out, not_38_out);
  and and_167 (and_167_out, and_159_out, not_41_out);
  and and_168 (and_168_out, and_160_out, not_41_out);
  and and_169 (and_169_out, and_161_out, not_41_out);
  // And and_170 has open pins: In_1=and_162_out, In_2=not_41_out, out=open
  or or_34 (or_34_out, Num_1[7], Num_1[6]);
  or or_35 (or_35_out, Num_1[5], Num_1[4]);
  or or_36 (or_36_out, Num_1[3], Num_1[2]);
  or or_37 (or_37_out, Num_1[1], Num_1[0]);
  or or_38 (or_38_out, or_34_out, or_35_out);
  or or_39 (or_39_out, or_38_out, or_40_out);
  or or_40 (or_40_out, or_36_out, or_37_out);
  or or_41 (or_41_out, and_168_out, or_42_out);
  or or_42 (or_42_out, and_167_out, and_163_out);
  or or_43 (or_43_out, and_169_out, or_44_out);
  or or_44 (or_44_out, and_173_out, or_48_out);
  or or_45 (or_45_out, or_44_out, or_43_out);
  or or_46 (or_46_out, and_165_out, and_167_out);
  or or_47 (or_47_out, and_166_out, and_168_out);
  or or_48 (or_48_out, and_172_out, or_50_out);
  or or_49 (Out_0, or_51_out, or_45_out);
  not not_42 (not_42_out, or_39_out);
  not not_43 (not_43_out, Num_1[7]);
  or or_50 (or_50_out, and_171_out, and_174_out);
  or or_51 (or_51_out, or_50_out, or_48_out);
  and and_171 (and_171_out, or_41_out, not_42_out);
  and and_172 (and_172_out, or_39_out, and_164_out);
  and and_173 (and_173_out, or_46_out, not_43_out);
  and and_174 (and_174_out, Num_1[7], or_47_out);
  xor xor_49 (xor_49_out, B_0[7], and_208_out);
  xor xor_50 (xor_50_out, B_0[6], and_208_out);
  xor xor_51 (xor_51_out, B_0[5], and_208_out);
  xor xor_52 (xor_52_out, B_0[4], and_208_out);
  xor xor_53 (xor_53_out, B_0[3], and_208_out);
  xor xor_54 (xor_54_out, B_0[2], and_208_out);
  xor xor_55 (xor_55_out, B_0[1], and_208_out);
  xor xor_56 (xor_56_out, B_0[0], and_208_out);
  and and_175 (and_194_out[0], B_0[0], A_0[0]);
  nand nand_345 (nand_352_out[0], B_0[0], A_0[0]);
  or or_52 (or_67_out[0], B_0[0], A_0[0]);
  nor nor_9 (nor_16_out[0], B_0[0], A_0[0]);
  xor xor_57 (xor_76_out[0], B_0[0], A_0[0]);
  and and_176 (and_194_out[1], B_0[1], A_0[1]);
  nand nand_346 (nand_352_out[1], B_0[1], A_0[1]);
  or or_53 (or_67_out[1], B_0[1], A_0[1]);
  nor nor_10 (nor_16_out[1], B_0[1], A_0[1]);
  xor xor_58 (xor_76_out[1], B_0[1], A_0[1]);
  and and_177 (and_194_out[2], B_0[2], A_0[2]);
  nand nand_347 (nand_352_out[2], B_0[2], A_0[2]);
  or or_54 (or_67_out[2], B_0[2], A_0[2]);
  nor nor_11 (nor_16_out[2], B_0[2], A_0[2]);
  xor xor_59 (xor_76_out[2], B_0[2], A_0[2]);
  and and_178 (and_194_out[3], B_0[3], A_0[3]);
  and and_179 (and_194_out[4], B_0[4], A_0[4]);
  nand nand_348 (nand_352_out[3], B_0[3], A_0[3]);
  nand nand_349 (nand_352_out[4], B_0[4], A_0[4]);
  or or_55 (or_67_out[3], B_0[3], A_0[3]);
  or or_56 (or_67_out[4], B_0[4], A_0[4]);
  nor nor_12 (nor_16_out[3], B_0[3], A_0[3]);
  nor nor_13 (nor_16_out[4], B_0[4], A_0[4]);
  xor xor_60 (xor_76_out[3], B_0[3], A_0[3]);
  xor xor_61 (xor_76_out[4], B_0[4], A_0[4]);
  and and_180 (and_194_out[5], B_0[5], A_0[5]);
  nand nand_350 (nand_352_out[5], B_0[5], A_0[5]);
  or or_57 (or_67_out[5], B_0[5], A_0[5]);
  nor nor_14 (nor_16_out[5], B_0[5], A_0[5]);
  xor xor_62 (xor_76_out[5], B_0[5], A_0[5]);
  and and_181 (and_181_out, xor_49_out, A_0[7]);
  xor xor_63 (xor_63_out, A_0[7], xor_49_out);
  and and_182 (and_182_out, xor_50_out, A_0[6]);
  xor xor_64 (xor_64_out, A_0[6], xor_50_out);
  and and_183 (and_183_out, xor_51_out, A_0[5]);
  xor xor_65 (xor_65_out, A_0[5], xor_51_out);
  and and_184 (and_184_out, xor_52_out, A_0[4]);
  xor xor_66 (xor_66_out, A_0[4], xor_52_out);
  and and_185 (and_185_out, xor_53_out, A_0[3]);
  xor xor_67 (xor_67_out, A_0[3], xor_53_out);
  and and_186 (and_186_out, xor_54_out, A_0[2]);
  xor xor_68 (xor_68_out, A_0[2], xor_54_out);
  and and_187 (and_187_out, xor_55_out, A_0[1]);
  xor xor_69 (xor_69_out, A_0[1], xor_55_out);
  and and_188 (and_188_out, xor_56_out, A_0[0]);
  xor xor_70 (xor_70_out, A_0[0], xor_56_out);
  and and_189 (and_194_out[6], B_0[6], A_0[6]);
  nand nand_351 (nand_352_out[6], B_0[6], A_0[6]);
  or or_58 (or_67_out[6], B_0[6], A_0[6]);
  nor nor_15 (nor_16_out[6], B_0[6], A_0[6]);
  xor xor_71 (xor_76_out[6], B_0[6], A_0[6]);
  or or_59 (or_59_out, and_181_out, and_190_out);
  and and_190 (and_190_out, xor_63_out, or_60_out);
  xor xor_72 (xor_80_out[7], xor_63_out, or_60_out);
  or or_60 (or_60_out, and_182_out, and_191_out);
  and and_191 (and_191_out, xor_64_out, or_61_out);
  xor xor_73 (xor_80_out[6], xor_64_out, or_61_out);
  or or_61 (or_61_out, and_183_out, and_192_out);
  and and_192 (and_192_out, xor_65_out, or_62_out);
  xor xor_74 (xor_80_out[5], xor_65_out, or_62_out);
  or or_62 (or_62_out, and_184_out, and_193_out);
  and and_193 (and_193_out, xor_66_out, or_63_out);
  xor xor_75 (xor_80_out[4], xor_66_out, or_63_out);
  or or_63 (or_63_out, and_185_out, and_195_out);
  or or_64 (or_64_out, and_186_out, and_196_out);
  or or_65 (or_65_out, and_187_out, and_197_out);
  or or_66 (or_66_out, and_188_out, and_198_out);
  and and_194 (and_194_out[7], B_0[7], A_0[7]);
  nand nand_352 (nand_352_out[7], B_0[7], A_0[7]);
  or or_67 (or_67_out[7], B_0[7], A_0[7]);
  nor nor_16 (nor_16_out[7], B_0[7], A_0[7]);
  xor xor_76 (xor_76_out[7], B_0[7], A_0[7]);
  and and_195 (and_195_out, xor_67_out, or_64_out);
  xor xor_77 (xor_80_out[3], xor_67_out, or_64_out);
  and and_196 (and_196_out, xor_68_out, or_65_out);
  xor xor_78 (xor_80_out[2], xor_68_out, or_65_out);
  and and_197 (and_197_out, xor_69_out, or_66_out);
  xor xor_79 (xor_80_out[1], xor_69_out, or_66_out);
  and and_198 (and_198_out, xor_70_out, and_208_out);
  xor xor_80 (xor_80_out[0], xor_70_out, and_208_out);
  assign C_Arith[0] = and_209_out ? and_194_out[0] : 1'bz;  // Driver driver_185
  assign C_Arith[1] = and_209_out ? and_194_out[1] : 1'bz;  // Driver driver_186
  assign C_Arith[0] = and_210_out ? nand_352_out[0] : 1'bz;  // Driver driver_187
  assign C_Arith[1] = and_210_out ? nand_352_out[1] : 1'bz;  // Driver driver_188
  assign C_Arith[0] = and_211_out ? or_67_out[0] : 1'bz;  // Driver driver_189
  assign C_Arith[1] = and_211_out ? or_67_out[1] : 1'bz;  // Driver driver_190
  assign C_Arith[0] = and_212_out ? nor_16_out[0] : 1'bz;  // Driver driver_191
  assign C_Arith[1] = and_212_out ? nor_16_out[1] : 1'bz;  // Driver driver_192
  assign C_Arith[0] = and_213_out ? xor_76_out[0] : 1'bz;  // Driver driver_193
  assign C_Arith[1] = and_213_out ? xor_76_out[1] : 1'bz;  // Driver driver_194
  assign C_Arith[2] = and_209_out ? and_194_out[2] : 1'bz;  // Driver driver_195
  assign C_Arith[3] = and_209_out ? and_194_out[3] : 1'bz;  // Driver driver_196
  assign C_Arith[2] = and_210_out ? nand_352_out[2] : 1'bz;  // Driver driver_197
  assign C_Arith[3] = and_210_out ? nand_352_out[3] : 1'bz;  // Driver driver_198
  assign C_Arith[2] = and_211_out ? or_67_out[2] : 1'bz;  // Driver driver_199
  assign C_Arith[3] = and_211_out ? or_67_out[3] : 1'bz;  // Driver driver_200
  assign C_Arith[2] = and_212_out ? nor_16_out[2] : 1'bz;  // Driver driver_201
  assign C_Arith[3] = and_212_out ? nor_16_out[3] : 1'bz;  // Driver driver_202
  assign C_Arith[2] = and_213_out ? xor_76_out[2] : 1'bz;  // Driver driver_203
  assign C_Arith[3] = and_213_out ? xor_76_out[3] : 1'bz;  // Driver driver_204
  assign C_Arith[4] = and_209_out ? and_194_out[4] : 1'bz;  // Driver driver_205
  assign C_Arith[5] = and_209_out ? and_194_out[5] : 1'bz;  // Driver driver_206
  assign C_Arith[4] = and_210_out ? nand_352_out[4] : 1'bz;  // Driver driver_207
  assign C_Arith[5] = and_210_out ? nand_352_out[5] : 1'bz;  // Driver driver_208
  assign C_Arith[4] = and_211_out ? or_67_out[4] : 1'bz;  // Driver driver_209
  assign C_Arith[5] = and_211_out ? or_67_out[5] : 1'bz;  // Driver driver_210
  assign C_Arith[4] = and_212_out ? nor_16_out[4] : 1'bz;  // Driver driver_211
  assign C_Arith[5] = and_212_out ? nor_16_out[5] : 1'bz;  // Driver driver_212
  assign C_Arith[4] = and_213_out ? xor_76_out[4] : 1'bz;  // Driver driver_213
  assign C_Arith[5] = and_213_out ? xor_76_out[5] : 1'bz;  // Driver driver_214
  assign C_Arith[6] = and_209_out ? and_194_out[6] : 1'bz;  // Driver driver_215
  assign C_Arith[7] = and_209_out ? and_194_out[7] : 1'bz;  // Driver driver_216
  assign C_Arith[6] = and_210_out ? nand_352_out[6] : 1'bz;  // Driver driver_217
  assign C_Arith[7] = and_210_out ? nand_352_out[7] : 1'bz;  // Driver driver_218
  assign C_Arith[6] = and_211_out ? or_67_out[6] : 1'bz;  // Driver driver_219
  assign C_Arith[7] = and_211_out ? or_67_out[7] : 1'bz;  // Driver driver_220
  assign C_Arith[6] = and_212_out ? nor_16_out[6] : 1'bz;  // Driver driver_221
  assign C_Arith[7] = and_212_out ? nor_16_out[7] : 1'bz;  // Driver driver_222
  assign C_Arith[6] = and_213_out ? xor_76_out[6] : 1'bz;  // Driver driver_223
  assign C_Arith[7] = and_213_out ? xor_76_out[7] : 1'bz;  // Driver driver_224
  not not_44 (not_44_out, C_2);
  assign C_Arith[0] = or_68_out ? xor_80_out[0] : 1'bz;  // Driver driver_225
  not not_45 (not_45_out, C_1);
  not not_46 (not_46_out, C_1);
  assign C_Arith[1] = or_68_out ? xor_80_out[1] : 1'bz;  // Driver driver_226
  assign C_Arith[2] = or_68_out ? xor_80_out[2] : 1'bz;  // Driver driver_227
  not not_47 (not_47_out, C_0);
  and and_199 (and_199_out, not_47_out, not_45_out);
  and and_200 (and_200_out, C_0, not_45_out);
  and and_201 (and_201_out, not_47_out, C_1);
  and and_202 (and_202_out, C_1, C_0);
  not not_48 (not_48_out, C_2);
  not not_49 (not_49_out, C_0);
  and and_203 (and_203_out, not_49_out, not_46_out);
  and and_204 (and_204_out, C_0, not_46_out);
  and and_205 (and_205_out, not_49_out, C_1);
  and and_206 (and_206_out, C_1, C_0);
  not not_50 (not_50_out, not_44_out);
  assign C_Arith[3] = or_68_out ? xor_80_out[3] : 1'bz;  // Driver driver_228
  assign C_Arith[4] = or_68_out ? xor_80_out[4] : 1'bz;  // Driver driver_229
  assign C_Arith[5] = or_68_out ? xor_80_out[5] : 1'bz;  // Driver driver_230
  assign C_Arith[6] = or_68_out ? xor_80_out[6] : 1'bz;  // Driver driver_231
  and and_207 (and_207_out, and_199_out, not_48_out);
  and and_208 (and_208_out, and_200_out, not_48_out);
  and and_209 (and_209_out, and_201_out, not_48_out);
  and and_210 (and_210_out, and_202_out, not_48_out);
  and and_211 (and_211_out, and_203_out, not_50_out);
  and and_212 (and_212_out, and_204_out, not_50_out);
  and and_213 (and_213_out, and_205_out, not_50_out);
  // And and_214 has open pins: In_1=and_206_out, In_2=not_50_out, out=open
  assign C_Arith[7] = or_68_out ? xor_80_out[7] : 1'bz;  // Driver driver_232
  or or_68 (or_68_out, and_207_out, and_208_out);
  // NotConnected on notconnected_9_out
  // NotConnected on notconnected_10_out
  // NotConnected on notconnected_11_out
  // NotConnected on notconnected_12_out
  // NotConnected on notconnected_13_out
  // NotConnected on notconnected_14_out
  // NotConnected on notconnected_15_out
  // NotConnected on notconnected_16_out
  // NotConnected on notconnected_17_out
  nand nand_353 (nand_353_out, nand_356_out, nand_354_out);
  nand nand_354 (nand_354_out, nand_353_out, notconnected_14_out);
  nand nand_355 (nand_355_out, nand_354_out, notconnected_14_out, nand_356_out);
  nand nand_356 (nand_356_out, nand_355_out, notconnected_9_out[6]);
  nand nand_357 (nand_357_out, nand_360_out, nand_358_out);
  nand nand_358 (nand_358_out, nand_357_out, notconnected_14_out);
  nand nand_359 (nand_359_out, nand_358_out, notconnected_14_out, nand_360_out);
  nand nand_360 (nand_360_out, nand_359_out, notconnected_9_out[4]);
  nand nand_361 (nand_361_out, nand_364_out, nand_362_out);
  nand nand_362 (nand_362_out, nand_361_out, notconnected_14_out);
  nand nand_363 (nand_363_out, nand_362_out, notconnected_14_out, nand_364_out);
  nand nand_364 (nand_364_out, nand_363_out, notconnected_9_out[2]);
  nand nand_365 (nand_365_out, nand_368_out, nand_366_out);
  nand nand_366 (nand_366_out, nand_365_out, notconnected_14_out);
  nand nand_367 (nand_367_out, nand_366_out, notconnected_14_out, nand_368_out);
  nand nand_368 (nand_368_out, nand_367_out, notconnected_9_out[0]);
  DipSwitch dipswitch_2 (.out(dipswitch_2_out));
  DipSwitch dipswitch_3 (.out(dipswitch_3_out));
  DipSwitch dipswitch_4 (.out(dipswitch_4_out));
  not not_51 (not_51_out, notconnected_12_out[7]);
  and and_215 (and_215_out, notconnected_10_out, notconnected_12_out[7]);
  not not_52 (not_52_out, notconnected_12_out[6]);
  and and_216 (and_216_out, notconnected_10_out, notconnected_12_out[6]);
  not not_53 (not_53_out, notconnected_12_out[5]);
  and and_217 (and_217_out, notconnected_10_out, notconnected_12_out[5]);
  not not_54 (not_54_out, notconnected_12_out[4]);
  and and_218 (and_218_out, notconnected_10_out, notconnected_12_out[4]);
  not not_55 (not_55_out, notconnected_12_out[3]);
  and and_219 (and_219_out, notconnected_10_out, notconnected_12_out[3]);
  not not_56 (not_56_out, notconnected_12_out[2]);
  and and_220 (and_220_out, notconnected_10_out, notconnected_12_out[2]);
  not not_57 (not_57_out, notconnected_12_out[1]);
  and and_221 (and_221_out, notconnected_10_out, notconnected_12_out[1]);
  not not_58 (not_58_out, notconnected_12_out[0]);
  and and_222 (and_222_out, notconnected_10_out, notconnected_12_out[0]);
  and and_223 (and_223_out, not_59_out, dipswitch_3_out);
  not not_59 (not_59_out, dipswitch_4_out);
  and and_224 (and_224_out, dipswitch_3_out, dipswitch_4_out);
  and and_225 (and_225_out, not_51_out, notconnected_10_out);
  and and_226 (and_226_out, not_52_out, notconnected_10_out);
  and and_227 (and_227_out, not_53_out, notconnected_10_out);
  and and_228 (and_228_out, not_54_out, notconnected_10_out);
  and and_229 (and_229_out, not_55_out, notconnected_10_out);
  and and_230 (and_230_out, not_56_out, notconnected_10_out);
  and and_231 (and_231_out, not_57_out, notconnected_10_out);
  and and_232 (and_232_out, not_58_out, notconnected_10_out);
  nand nand_369 (nand_369_out, nand_354_out, nand_370_out);
  nand nand_370 (nand_370_out, nand_369_out, nand_355_out);
  nand nand_371 (nand_371_out, nand_358_out, nand_372_out);
  nand nand_372 (nand_372_out, nand_371_out, nand_359_out);
  nand nand_373 (nand_373_out, nand_362_out, nand_374_out);
  nand nand_374 (nand_374_out, nand_373_out, nand_363_out);
  nand nand_375 (nand_375_out, nand_366_out, nand_376_out);
  nand nand_376 (nand_376_out, nand_375_out, nand_367_out);
  nor nor_17 (nor_17_out, and_225_out, nor_18_out);
  nor nor_18 (nor_18_out, nor_17_out, and_215_out);
  nor nor_19 (nor_19_out, and_226_out, nor_20_out);
  nor nor_20 (nor_20_out, nor_19_out, and_216_out);
  nor nor_21 (nor_21_out, and_227_out, nor_22_out);
  nor nor_22 (nor_22_out, nor_21_out, and_217_out);
  nor nor_23 (nor_23_out, and_228_out, nor_24_out);
  nor nor_24 (nor_24_out, nor_23_out, and_218_out);
  nor nor_25 (nor_25_out, and_229_out, nor_26_out);
  nor nor_26 (nor_26_out, nor_25_out, and_219_out);
  nor nor_27 (nor_27_out, and_230_out, nor_28_out);
  nor nor_28 (nor_28_out, nor_27_out, and_220_out);
  nor nor_29 (nor_29_out, and_231_out, nor_30_out);
  nor nor_30 (nor_30_out, nor_29_out, and_221_out);
  nor nor_31 (nor_31_out, and_232_out, nor_32_out);
  nor nor_32 (nor_32_out, nor_31_out, and_222_out);
  assign driver_233_out = notconnected_15_out ? nand_369_out : 1'bz;  // Driver driver_233
  assign driver_234_out = notconnected_16_out ? nand_369_out : 1'bz;  // Driver driver_234
  assign driver_235_out = notconnected_15_out ? nand_371_out : 1'bz;  // Driver driver_235
  assign driver_236_out = notconnected_16_out ? nand_371_out : 1'bz;  // Driver driver_236
  assign driver_237_out = notconnected_15_out ? nand_373_out : 1'bz;  // Driver driver_237
  assign driver_238_out = notconnected_16_out ? nand_373_out : 1'bz;  // Driver driver_238
  assign driver_239_out = notconnected_15_out ? nand_375_out : 1'bz;  // Driver driver_239
  assign driver_240_out = notconnected_16_out ? nand_375_out : 1'bz;  // Driver driver_240
  and and_233 (and_233_out, notconnected_13_out[7], notconnected_17_out[7]);
  xor xor_81 (xor_81_out, notconnected_17_out[7], notconnected_13_out[7]);
  and and_234 (and_234_out, notconnected_13_out[6], notconnected_17_out[6]);
  xor xor_82 (xor_82_out, notconnected_17_out[6], notconnected_13_out[6]);
  and and_235 (and_235_out, notconnected_13_out[5], notconnected_17_out[5]);
  xor xor_83 (xor_83_out, notconnected_17_out[5], notconnected_13_out[5]);
  and and_236 (and_236_out, notconnected_13_out[4], notconnected_17_out[4]);
  xor xor_84 (xor_84_out, notconnected_17_out[4], notconnected_13_out[4]);
  and and_237 (and_237_out, notconnected_13_out[3], notconnected_17_out[3]);
  xor xor_85 (xor_85_out, notconnected_17_out[3], notconnected_13_out[3]);
  and and_238 (and_238_out, notconnected_13_out[2], notconnected_17_out[2]);
  xor xor_86 (xor_86_out, notconnected_17_out[2], notconnected_13_out[2]);
  and and_239 (and_239_out, notconnected_13_out[1], notconnected_17_out[1]);
  xor xor_87 (xor_87_out, notconnected_17_out[1], notconnected_13_out[1]);
  and and_240 (and_240_out, notconnected_13_out[0], notconnected_17_out[0]);
  xor xor_88 (xor_88_out, notconnected_17_out[0], notconnected_13_out[0]);
  nor nor_33 (nor_33_out, and_223_out, nor_34_out);
  nor nor_34 (nor_34_out, nor_33_out, and_224_out);
  or or_69 (or_69_out, and_233_out, and_241_out);
  and and_241 (and_241_out, xor_81_out, or_70_out);
  xor xor_89 (xor_89_out, xor_81_out, or_70_out);
  or or_70 (or_70_out, and_234_out, and_242_out);
  and and_242 (and_242_out, xor_82_out, or_71_out);
  xor xor_90 (xor_90_out, xor_82_out, or_71_out);
  or or_71 (or_71_out, and_235_out, and_243_out);
  and and_243 (and_243_out, xor_83_out, or_72_out);
  xor xor_91 (xor_91_out, xor_83_out, or_72_out);
  or or_72 (or_72_out, and_236_out, and_244_out);
  and and_244 (and_244_out, xor_84_out, or_73_out);
  xor xor_92 (xor_92_out, xor_84_out, or_73_out);
  or or_73 (or_73_out, and_237_out, and_253_out);
  or or_74 (or_74_out, and_238_out, and_254_out);
  or or_75 (or_75_out, and_239_out, and_255_out);
  or or_76 (or_76_out, and_240_out, and_256_out);
  // NotConnected on notconnected_18_out
  Reset reset_1 ();  // open: out
  Reset reset_2 ();  // open: out
  and and_245 (and_245_out, nor_17_out, notconnected_11_out);
  Reset reset_3 ();  // open: out
  and and_246 (and_246_out, nor_19_out, notconnected_11_out);
  Reset reset_4 ();  // open: out
  and and_247 (and_247_out, nor_21_out, notconnected_11_out);
  Reset reset_5 ();  // open: out
  and and_248 (and_248_out, nor_23_out, notconnected_11_out);
  Reset reset_6 ();  // open: out
  and and_249 (and_249_out, nor_25_out, notconnected_11_out);
  Reset reset_7 ();  // open: out
  and and_250 (and_250_out, nor_27_out, notconnected_11_out);
  Reset reset_8 ();  // open: out
  and and_251 (and_251_out, nor_29_out, notconnected_11_out);
  Reset reset_9 ();  // open: out
  and and_252 (and_252_out, nor_31_out, notconnected_11_out);
  and and_253 (and_253_out, xor_85_out, or_74_out);
  xor xor_93 (xor_93_out, xor_85_out, or_74_out);
  and and_254 (and_254_out, xor_86_out, or_75_out);
  xor xor_94 (xor_94_out, xor_86_out, or_75_out);
  and and_255 (and_255_out, xor_87_out, or_76_out);
  xor xor_95 (xor_95_out, xor_87_out, or_76_out);
  and and_256 (and_256_out, xor_88_out, notconnected_18_out);
  xor xor_96 (xor_96_out, xor_88_out, notconnected_18_out);
  and and_257 (and_257_out, nor_33_out, dipswitch_2_out);
  nand nand_377 (nand_377_out, nand_380_out, nand_378_out);
  nand nand_378 (nand_378_out, nand_377_out, notconnected_14_out);
  nand nand_379 (nand_379_out, nand_378_out, notconnected_14_out, nand_380_out);
  nand nand_380 (nand_380_out, nand_379_out, notconnected_9_out[7]);
  nand nand_381 (nand_381_out, nand_384_out, nand_382_out);
  nand nand_382 (nand_382_out, nand_381_out, notconnected_14_out);
  nand nand_383 (nand_383_out, nand_382_out, notconnected_14_out, nand_384_out);
  nand nand_384 (nand_384_out, nand_383_out, notconnected_9_out[5]);
  nand nand_385 (nand_385_out, nand_388_out, nand_386_out);
  nand nand_386 (nand_386_out, nand_385_out, notconnected_14_out);
  nand nand_387 (nand_387_out, nand_386_out, notconnected_14_out, nand_388_out);
  nand nand_388 (nand_388_out, nand_387_out, notconnected_9_out[3]);
  nand nand_389 (nand_389_out, nand_392_out, nand_390_out);
  nand nand_390 (nand_390_out, nand_389_out, notconnected_14_out);
  nand nand_391 (nand_391_out, nand_390_out, notconnected_14_out, nand_392_out);
  nand nand_392 (nand_392_out, nand_391_out, notconnected_9_out[1]);
  nand nand_393 (nand_393_out, nand_378_out, nand_394_out);
  nand nand_394 (nand_394_out, nand_393_out, nand_379_out);
  nand nand_395 (nand_395_out, nand_382_out, nand_396_out);
  nand nand_396 (nand_396_out, nand_395_out, nand_383_out);
  nand nand_397 (nand_397_out, nand_386_out, nand_398_out);
  nand nand_398 (nand_398_out, nand_397_out, nand_387_out);
  nand nand_399 (nand_399_out, nand_390_out, nand_400_out);
  nand nand_400 (nand_400_out, nand_399_out, nand_391_out);
  assign driver_241_out = notconnected_15_out ? nand_393_out : 1'bz;  // Driver driver_241
  assign driver_242_out = notconnected_16_out ? nand_393_out : 1'bz;  // Driver driver_242
  assign driver_243_out = notconnected_15_out ? nand_395_out : 1'bz;  // Driver driver_243
  assign driver_244_out = notconnected_16_out ? nand_395_out : 1'bz;  // Driver driver_244
  assign driver_245_out = notconnected_15_out ? nand_397_out : 1'bz;  // Driver driver_245
  assign driver_246_out = notconnected_16_out ? nand_397_out : 1'bz;  // Driver driver_246
  assign driver_247_out = notconnected_15_out ? nand_399_out : 1'bz;  // Driver driver_247
  assign driver_248_out = notconnected_16_out ? nand_399_out : 1'bz;  // Driver driver_248
  // NotConnected on notconnected_19_out
  // NotConnected on notconnected_20_out
  // NotConnected on notconnected_21_out
  // NotConnected on notconnected_22_out
  and and_258 (and_258_out, notconnected_20_out[0], notconnected_20_out[0]);
  or or_77 (or_77_out, notconnected_21_out[0], notconnected_21_out[0]);
  xor xor_97 (xor_97_out, notconnected_22_out[0], notconnected_22_out[0]);
  and and_259 (and_259_out, notconnected_20_out[1], notconnected_20_out[1]);
  or or_78 (or_78_out, notconnected_21_out[1], notconnected_21_out[1]);
  xor xor_98 (xor_98_out, notconnected_22_out[1], notconnected_22_out[1]);
  not not_60 (not_60_out, notconnected_23_out);
  // NotConnected on notconnected_23_out
  and and_260 (and_260_out, notconnected_20_out[2], notconnected_20_out[2]);
  and and_261 (and_261_out, notconnected_20_out[3], notconnected_20_out[3]);
  or or_79 (or_79_out, notconnected_21_out[2], notconnected_21_out[2]);
  or or_80 (or_80_out, notconnected_21_out[3], notconnected_21_out[3]);
  xor xor_99 (xor_99_out, notconnected_22_out[2], notconnected_22_out[2]);
  xor xor_100 (xor_100_out, notconnected_22_out[3], notconnected_22_out[3]);
  // And and_262 has open pins: In_1=and_263_out, In_2=notconnected_19_out[7], out=open
  xor xor_101 (xor_101_out, notconnected_19_out[7], and_263_out);
  and and_263 (and_263_out, and_264_out, notconnected_19_out[6]);
  xor xor_102 (xor_102_out, notconnected_19_out[6], and_264_out);
  and and_264 (and_264_out, and_265_out, notconnected_19_out[5]);
  xor xor_103 (xor_103_out, notconnected_19_out[5], and_265_out);
  and and_265 (and_265_out, and_266_out, notconnected_19_out[4]);
  xor xor_104 (xor_104_out, notconnected_19_out[4], and_266_out);
  and and_266 (and_266_out, and_267_out, notconnected_19_out[3]);
  xor xor_105 (xor_105_out, notconnected_19_out[3], and_267_out);
  and and_267 (and_267_out, and_268_out, notconnected_19_out[2]);
  xor xor_106 (xor_106_out, notconnected_19_out[2], and_268_out);
  and and_268 (and_268_out, and_269_out, notconnected_19_out[1]);
  xor xor_107 (xor_107_out, notconnected_19_out[1], and_269_out);
  and and_269 (and_269_out, not_60_out, notconnected_19_out[0]);
  xor xor_108 (xor_108_out, notconnected_19_out[0], not_60_out);
  and and_270 (and_270_out, notconnected_20_out[4], notconnected_20_out[4]);
  or or_81 (or_81_out, notconnected_21_out[4], notconnected_21_out[4]);
  xor xor_109 (xor_109_out, notconnected_22_out[4], notconnected_22_out[4]);
  and and_271 (and_271_out, notconnected_20_out[5], notconnected_20_out[5]);
  or or_82 (or_82_out, notconnected_21_out[5], notconnected_21_out[5]);
  xor xor_110 (xor_110_out, notconnected_22_out[5], notconnected_22_out[5]);
  and and_272 (and_272_out, notconnected_20_out[6], notconnected_20_out[6]);
  and and_273 (and_273_out, notconnected_20_out[7], notconnected_20_out[7]);
  or or_83 (or_83_out, notconnected_21_out[6], notconnected_21_out[6]);
  or or_84 (or_84_out, notconnected_21_out[7], notconnected_21_out[7]);
  xor xor_111 (xor_111_out, notconnected_22_out[6], notconnected_22_out[6]);
  xor xor_112 (xor_112_out, notconnected_22_out[7], notconnected_22_out[7]);
  // NotConnected on notconnected_24_out
  // NotConnected on notconnected_25_out
  // NotConnected on notconnected_26_out
  // NotConnected on notconnected_27_out
  // NotConnected on notconnected_28_out
  // NotConnected on notconnected_29_out
  and and_274 (and_274_out, notconnected_30_out, notconnected_24_out[0]);
  nand nand_401 (nand_401_out, notconnected_25_out[0], notconnected_25_out[0]);
  nor nor_35 (nor_35_out, notconnected_26_out[0], notconnected_26_out[0]);
  not not_61 (not_61_out, notconnected_29_out);
  and and_275 (and_275_out, notconnected_30_out, notconnected_24_out[1]);
  and and_276 (and_276_out, notconnected_30_out, notconnected_24_out[2]);
  nand nand_402 (nand_402_out, notconnected_25_out[1], notconnected_25_out[1]);
  nand nand_403 (nand_403_out, notconnected_25_out[2], notconnected_25_out[2]);
  nor nor_36 (nor_36_out, notconnected_26_out[1], notconnected_26_out[1]);
  nor nor_37 (nor_37_out, notconnected_26_out[2], notconnected_26_out[2]);
  not not_62 (not_62_out, notconnected_28_out);
  not not_63 (not_63_out, notconnected_27_out);
  not not_64 (not_64_out, notconnected_29_out);
  not not_65 (not_65_out, notconnected_28_out);
  not not_66 (not_66_out, notconnected_27_out);
  not not_67 (not_67_out, not_61_out);
  // NotConnected on notconnected_30_out
  and and_277 (and_277_out, notconnected_30_out, notconnected_24_out[3]);
  nand nand_404 (nand_404_out, notconnected_25_out[3], notconnected_25_out[3]);
  nor nor_38 (nor_38_out, notconnected_26_out[3], notconnected_26_out[3]);
  and and_278 (and_278_out, not_63_out, not_62_out);
  and and_279 (and_279_out, notconnected_27_out, not_62_out);
  and and_280 (and_280_out, not_63_out, notconnected_28_out);
  and and_281 (and_281_out, notconnected_28_out, notconnected_27_out);
  and and_282 (and_282_out, not_66_out, not_65_out);
  and and_283 (and_283_out, notconnected_27_out, not_65_out);
  and and_284 (and_284_out, not_66_out, notconnected_28_out);
  and and_285 (and_285_out, notconnected_28_out, notconnected_27_out);
  and and_286 (and_286_out, notconnected_30_out, notconnected_24_out[4]);
  nand nand_405 (nand_405_out, notconnected_25_out[4], notconnected_25_out[4]);
  nor nor_39 (nor_39_out, notconnected_26_out[4], notconnected_26_out[4]);
  and and_287 (and_287_out, and_278_out, not_64_out);
  and and_288 (and_288_out, and_279_out, not_64_out);
  and and_289 (and_289_out, and_280_out, not_64_out);
  and and_290 (and_290_out, and_281_out, not_64_out);
  and and_291 (and_291_out, and_282_out, not_67_out);
  and and_292 (and_292_out, and_283_out, not_67_out);
  and and_293 (and_293_out, and_284_out, not_67_out);
  and and_294 (and_294_out, and_285_out, not_67_out);
  and and_295 (and_295_out, notconnected_30_out, notconnected_24_out[5]);
  and and_296 (and_296_out, notconnected_30_out, notconnected_24_out[6]);
  nand nand_406 (nand_406_out, notconnected_25_out[5], notconnected_25_out[5]);
  nand nand_407 (nand_407_out, notconnected_25_out[6], notconnected_25_out[6]);
  nor nor_40 (nor_40_out, notconnected_26_out[5], notconnected_26_out[5]);
  nor nor_41 (nor_41_out, notconnected_26_out[6], notconnected_26_out[6]);
  and and_297 (and_297_out, notconnected_30_out, notconnected_24_out[7]);
  nand nand_408 (nand_408_out, notconnected_25_out[7], notconnected_25_out[7]);
  nor nor_42 (nor_42_out, notconnected_26_out[7], notconnected_26_out[7]);
  // NotConnected on notconnected_31_out
  assign driver_249_out = notconnected_32_out ? notconnected_31_out[0] : 1'bz;  // Driver driver_249
  assign driver_250_out = notconnected_32_out ? notconnected_31_out[1] : 1'bz;  // Driver driver_250
  assign driver_251_out = notconnected_32_out ? notconnected_31_out[2] : 1'bz;  // Driver driver_251
  assign driver_252_out = notconnected_32_out ? notconnected_31_out[3] : 1'bz;  // Driver driver_252
  assign driver_253_out = notconnected_32_out ? notconnected_31_out[4] : 1'bz;  // Driver driver_253
  assign driver_254_out = notconnected_32_out ? notconnected_31_out[5] : 1'bz;  // Driver driver_254
  assign driver_255_out = notconnected_32_out ? notconnected_31_out[6] : 1'bz;  // Driver driver_255
  // NotConnected on notconnected_32_out
  assign driver_256_out = notconnected_32_out ? notconnected_31_out[7] : 1'bz;  // Driver driver_256

  // Notes on the sheet:
  //   DESTINATION sel
  //   Disable
  //   A_1
  //   A_0
  //   2x4 Demux
  //   Operation Decode
  //   Add
  //   Sub
  //   AND
  //   NAND
  //   OR
  //   NOR
  //   XOR
  //   Unused
  //   A3
  //   Immediate Arg 1
  //   Immediate Arg 2
  //   Arithmetic/Compare
  //   RAM
  //   Argument
  //   Arithmetic arguments
  //   A1
  //   A2
  //   3x8 Demux
  //   Arguments are listsed in order in decimal value
  //   Is0
  //   IsNot0
  //   More
  //   Less
  //   MoreOrEqual
  //   LessOrEqual
  //   Always
  //   Never
  //   Compare arguments
  //   ARG2 sel
  //   Many components are designed to
  //   take OPCODEs in and only use the
  //   last 3 argument bits.
  //   Arithmetic
  //   Compare
  //   Ram
  //   Main OPCODE Line
  //   ARG1 sel
  //   Immediates
  //   ARG2
  //   Immediate 2 Enable
  //   ARG1
  //   Immediate 1 Enable
  //   Immediate's Disable the corresponding argument sel
  //   Input
  //   Z SWITCH
  //   Edge Register
  //   Clk
  //   Load A
  //   Load B
  //   D
  //   Load
  //   Edge Flop
  //   Latch
  //   Loaded
  //   B
  //   A
  //   ALU
  //   ADDER
  //   .
  //   Overwrite Value
  //   Overwrite
  //   Step
  //   COUNTER
  //   Select
  //   MUX
  //   SWITCH
  //   Conditional Unit
  //   Is less than 0 Unit
  //   Is!0 Unit
  //   COMPONENTS
  //   Register - outdated
  //   Save
  //   Save Value
  //   1 Bit mem
  //   SaveVal
  //   Reset
  //   Write
  //   Always OUT
  //   OUT
  //   Always On Out
  //   Out
  //   INCRMNT
  //   SWITCH FAKE
endmodule

/* Test case:
D C L ALWAYS LOADED
# 1. Randomized Startup: Register state is unknown (X). LOADED is 0 because L=0.
0x00 0 0 X 0x00

# 2. Load 0xAA: ALWAYS updates to 0xAA. LOADED shows it because L=1.
0xAA C 1 0xAA 0xAA

# 3. Transparent Check: ALWAYS stays 0xAA. LOADED drops to 0x00 because L=0.
0x55 0 0 0xAA 0x00
0x21 C 0 0x21 0x00

# 5. Load 0x00: Register becomes 0. Both pins show 0.
0x00 C 1 0x00 0x00

# 6. Edge-Triggering: Data 0xEE only moves to ALWAYS on the rising edge.
0xEE 0 1 0x00 0x00  # L=1, but no clock yet; LOADED is 0 because reg is 0
0xEE 1 1 0xEE 0xEE  # Clock goes high; Reg becomes 0xEE. LOADED now shows it.
0xDD 0 1 0xEE 0xEE  # Clock falls; Reg stays 0xEE.

# 7. High-Clock Stability Test
0xAA 0 1 0xEE 0xEE  # Prepare data 0xAA, but clock is 0. ALWAYS stays 0xEE.
0xAA 1 1 0xAA 0xAA  # Clock goes High. Register captures 0xAA.
0xFF 1 1 0xAA 0xAA  # DATA CHANGES TO 0xFF WHILE CLOCK IS STILL HIGH.
                    # ALWAYS MUST STAY 0xAA. If it changes to 0xFF, it's a latch!
*/

/* Test case:
C_2 C_1 C_0 A_0 B_0 C_Arith
0 0 0 9 6 15 #addition and subtraction
0 0 1 9 6 3
0 0 0 6 7 13
0 0 1 111 67 44
0 0 0 32 59 91
0 1 0 51 60 48  #and
0 1 0 3 2 2
0 1 0 5 3 1
0 1 0 12 25 8
0 1 0 4 8 0
1 0 0 5 3 7 #or
1 0 0 2 8 10
1 0 0 12 25 29
1 0 0 0 7 7
0 1 1 1 1 254 #nand
0 1 1 2 4 255
0 1 1 15 3 252
1 0 1 1 0 254 #nor
1 0 1 3 5 248
1 0 1 128 64 63
1 1 0 5 3 6 #xor
1 1 0 10 10 0
1 1 0 85 170 255
1 1 0 14 1 15
*/

/* Test case:
In_3 In_2 In_1 Num_1 Out_0
0 0 0 4 0
0 0 1 5 1
0 0 0 210 0
0 0 1 253 1
0 1 1 65 0
0 1 0 102 1
0 1 1 237 1
0 1 0 179 0
1 0 0 102 1
1 0 0 0 1
1 0 0 252 0
1 0 1 179 1
1 0 1 0 1
1 0 1 112 0
1 1 0 0 1
1 1 0 243 1
1 1 0 123 1
1 1 1 0 0
1 1 1 243 0
1 1 1 123 0
*/
